// Logisim project y86.circ as structural Verilog: 34 circuits, main circuit main
module main (
  input  in_1,
  input  in_2,
  input  in_3,
  input  [31:0] in_4,
  input  in_5,
  output [31:0] out_6,
  output [31:0] out_7,
  output [3:0] out_8,
  output [3:0] out_9,
  output [3:0] out_10,
  output [3:0] out_11,
  output [3:0] out_12,
  output [31:0] out_13,
  output [31:0] out_14,
  output [31:0] out_15,
  output [31:0] out_16,
  output [31:0] out_17
);

  wire clock_1_out, clock_2_out, cond_1_out_3, instr_valid_1_out_2, mem_read_1_out_2, mem_write_1_out_2,
       multiplexer_1_out, multiplexer_2_out, multiplexer_4_out, multiplexer_6_out, need_reg_1_out_2,
       need_valc_1_out_2, set_cc_1_out_2;
  wire [2:0] alu_1_out_8, cc_1_out_4, stat_1_out_3;
  wire [3:0] align_1_out_5, align_1_out_6, alufun_1_out_3, instr_mem_1_out_9, instr_mem_1_out_10,
       instr_mem_1_out_11;
  wire [31:0] adder_1_out, align_1_out_7, alu_1_out_7, alua_1_out_4, alub_1_out_3, and_1_out, and_2_out,
       and_3_out, and_4_out, and_5_out, and_6_out, and_7_out, and_8_out, and_9_out, and_10_out, and_11_out,
       and_12_out, and_13_out, and_14_out, and_15_out, and_16_out, and_17_out, and_18_out, and_19_out,
       and_20_out, and_21_out, and_22_out, and_23_out, and_24_out, and_25_out, and_26_out, and_27_out,
       and_28_out, and_29_out, and_30_out, and_31_out, and_32_out, bit_extender_1_out, instr_mem_1_out_7,
       mem_addr_1_out_4, mem_data_1_out_4, multiplexer_3_out, multiplexer_5_out, n32bit_ram_1_out_7,
       register_2_q, register_3_q, register_4_q, register_5_q, register_6_q, register_7_q, register_8_q,
       register_9_q, register_10_q, register_11_q, register_12_q, register_13_q, register_14_q,
       register_15_q, register_16_q, register_17_q, register_18_q, register_19_q, register_20_q,
       register_21_q, register_22_q, register_23_q, register_24_q, register_25_q, register_26_q,
       register_27_q, register_28_q, register_29_q, register_30_q, register_31_q, register_32_q,
       register_33_q;

  Clock clock_1 (.out(clock_1_out));
  DotMatrix #(.matrixcols(3), .matrixrows(1)) dotmatrix_1 (
    .col0(stat_1_out_3[2]), .col1(stat_1_out_3[1]), .col2(stat_1_out_3[0]));
  stat stat_1 (.out_3(stat_1_out_3), .in_1(instr_valid_1_out_2), .in_2(out_12));
  instr_valid instr_valid_1 (.out_2(instr_valid_1_out_2), .in_1(out_12));
  assign bit_extender_1_out = {{31{in_5}}, in_5};  // Bit_Extender bit_extender_1
  mem_read mem_read_1 (.out_2(mem_read_1_out_2), .in_1(out_12));
  mem_write mem_write_1 (.out_2(mem_write_1_out_2), .in_1(out_12));
  cond cond_1 (.in_1(cc_1_out_4), .out_3(cond_1_out_3), .in_2(instr_mem_1_out_9));
  cc cc_1 (.in_2(set_cc_1_out_2), .in_1(alu_1_out_8), .out_4(cc_1_out_4), .in_3(clock_2_out));
  ALU alu_1 (
    .out_7(alu_1_out_7), .in_1(alua_1_out_4), .in_2(alub_1_out_3), .out_8(alu_1_out_8),
    .in_3(alufun_1_out_3[3]), .in_4(alufun_1_out_3[2]), .in_5(alufun_1_out_3[1]), .in_6(alufun_1_out_3[0]));  // open: out_9
  set_cc set_cc_1 (.out_2(set_cc_1_out_2), .in_1(out_12));
  aluA alua_1 (.out_4(alua_1_out_4), .in_3(out_12), .in_2(align_1_out_7), .in_1(out_6));
  dstE dste_1 (.in_1(cond_1_out_3), .out_4(out_8), .in_3(out_12), .in_2(align_1_out_6));
  align align_1 (
    .in_1(need_reg_1_out_2), .out_5(align_1_out_5), .out_6(align_1_out_6), .out_7(align_1_out_7),
    .in_2(instr_mem_1_out_10), .in_3(instr_mem_1_out_11), .in_4(instr_mem_1_out_7));
  Multiplexer #(.enable("false")) multiplexer_1 (
    .in0(clock_2_out), .in1(clock_1_out), .out(multiplexer_1_out), .sel(in_2));
  instr_mem instr_mem_1 (
    .out_7(instr_mem_1_out_7), .out_10(instr_mem_1_out_10), .out_11(instr_mem_1_out_11), .out_8(out_12),
    .out_9(instr_mem_1_out_9), .in_1(multiplexer_1_out), .in_4(out_14), .in_2(in_2), .in_3(in_3),
    .in_6(out_17), .in_5(out_16));
  pc pc_1 (.out_4(out_14), .in_2(out_15), .in_3(clock_2_out), .in_1(in_1));
  Register #(.width(32)) register_1 (.D(adder_1_out), .Q(out_16), .clk(clock_1_out), .clr(in_3));  // open: en
  Adder #(.width(32)) adder_1 (.a(out_16), .b(in_4), .out(adder_1_out));  // open: cin, cout
  new_pc new_pc_1 (
    .out_6(out_15), .in_1(out_12), .in_2(align_1_out_7), .in_3(cond_1_out_3), .in_4(n32bit_ram_1_out_7),
    .in_5(out_13));
  Multiplexer #(.enable("false")) multiplexer_2 (
    .in0(mem_read_1_out_2), .in1(1'b0), .out(multiplexer_2_out), .sel(in_2));
  Multiplexer #(.width(32), .enable("false")) multiplexer_3 (
    .in0(mem_addr_1_out_4), .in1(out_16), .out(multiplexer_3_out), .sel(in_2));
  Multiplexer #(.enable("false")) multiplexer_4 (
    .in0(mem_write_1_out_2), .in1(in_2), .out(multiplexer_4_out), .sel(in_2));
  mem_addr mem_addr_1 (.out_4(mem_addr_1_out_4), .in_3(out_12), .in_1(alu_1_out_7), .in_2(out_6));
  aluB alub_1 (.out_3(alub_1_out_3), .in_2(out_12), .in_1(out_7));
  alufun alufun_1 (.out_3(alufun_1_out_3), .in_2(out_12), .in_1(instr_mem_1_out_9));
  RegisterFile registerfile_1 (
    .in_3(out_10), .in_4(out_8), .out_9(out_6), .out_10(out_7), .in_2(n32bit_ram_1_out_7), .in_1(out_11),
    .in_6(alu_1_out_7), .in_8(clock_2_out), .in_7(out_9), .in_5(in_1));
  srcA srca_1 (.out_3(out_11), .in_2(out_12), .in_1(align_1_out_5));
  dstM dstm_1 (.out_3(out_10), .in_2(out_12), .in_1(align_1_out_5));
  assign and_1_out = register_2_q & 32'h8430;  // AND_Gate and_1, 32 bits wide
  Register #(.width(32)) register_2 (
    .D(bit_extender_1_out), .Q(register_2_q), .clk(clock_1_out), .clr(in_3));  // open: en
  _32bit_RAM u_32bit_ram_1 (
    .in_5(multiplexer_6_out), .in_4(multiplexer_3_out), .in_1(multiplexer_2_out), .in_3(in_3),
    .in_6(multiplexer_5_out), .out_7(n32bit_ram_1_out_7), .in_2(multiplexer_4_out));  // open: out_8
  Multiplexer #(.width(32), .enable("false")) multiplexer_5 (
    .in0(mem_data_1_out_4), .in1(out_17), .out(multiplexer_5_out), .sel(in_2));
  mem_data mem_data_1 (.out_4(mem_data_1_out_4), .in_3(out_12), .in_1(out_6), .in_2(out_13));
  srcB srcb_1 (.out_3(out_9), .in_2(out_12), .in_1(align_1_out_6));
  need_valC need_valc_1 (.out_2(need_valc_1_out_2), .in_1(out_12));
  pc_inc pc_inc_1 (.in_1(need_valc_1_out_2), .in_2(need_reg_1_out_2), .out_4(out_13), .in_3(out_14));
  need_reg need_reg_1 (.out_2(need_reg_1_out_2), .in_1(out_12));
  assign and_2_out = register_3_q & 32'h85300001;  // AND_Gate and_2, 32 bits wide
  Register #(.width(32)) register_3 (.D(register_2_q), .Q(register_3_q), .clk(clock_1_out), .clr(in_3));  // open: en
  Multiplexer #(.enable("false")) multiplexer_6 (
    .in0(clock_2_out), .in1(clock_1_out), .out(multiplexer_6_out), .sel(in_2));
  Register #(.width(32)) register_4 (.D(register_3_q), .Q(register_4_q), .clk(clock_1_out), .clr(in_3));  // open: en
  Clock clock_2 (.out(clock_2_out));
  assign and_3_out = register_4_q & 32'h10000;  // AND_Gate and_3, 32 bits wide
  assign and_4_out = register_5_q & 32'h70;  // AND_Gate and_4, 32 bits wide
  Register #(.width(32)) register_5 (.D(register_4_q), .Q(register_5_q), .clk(clock_1_out), .clr(in_3));  // open: en
  assign and_5_out = register_6_q & 32'h24;  // AND_Gate and_5, 32 bits wide
  Register #(.width(32)) register_6 (.D(register_5_q), .Q(register_6_q), .clk(clock_1_out), .clr(in_3));  // open: en
  Register #(.width(32)) register_7 (.D(register_6_q), .Q(register_7_q), .clk(clock_1_out), .clr(in_3));  // open: en
  assign and_6_out = register_7_q & 32'hd000000;  // AND_Gate and_6, 32 bits wide
  assign and_7_out = register_8_q & 32'hc0000000;  // AND_Gate and_7, 32 bits wide
  Register #(.width(32)) register_8 (.D(register_7_q), .Q(register_8_q), .clk(clock_1_out), .clr(in_3));  // open: en
  Register #(.width(32)) register_9 (.D(register_8_q), .Q(register_9_q), .clk(clock_1_out), .clr(in_3));  // open: en
  assign and_8_out = register_9_q & 32'hb0000;  // AND_Gate and_8, 32 bits wide
  assign and_9_out = register_10_q & 32'ha00000;  // AND_Gate and_9, 32 bits wide
  Register #(.width(32)) register_10 (.D(register_9_q), .Q(register_10_q), .clk(clock_1_out), .clr(in_3));  // open: en
  assign and_10_out = register_11_q & 32'h8030;  // AND_Gate and_10, 32 bits wide
  Register #(.width(32)) register_11 (.D(register_10_q), .Q(register_11_q), .clk(clock_1_out), .clr(in_3));  // open: en
  Register #(.width(32)) register_12 (.D(register_11_q), .Q(register_12_q), .clk(clock_1_out), .clr(in_3));  // open: en
  assign and_11_out = register_12_q & 32'h8a00400;  // AND_Gate and_11, 32 bits wide
  assign and_12_out = register_13_q & 32'h8230;  // AND_Gate and_12, 32 bits wide
  Register #(.width(32)) register_13 (.D(register_12_q), .Q(register_13_q), .clk(clock_1_out), .clr(in_3));  // open: en
  assign and_13_out = register_14_q & 32'h28a01400;  // AND_Gate and_13, 32 bits wide
  Register #(.width(32)) register_14 (.D(register_13_q), .Q(register_14_q), .clk(clock_1_out), .clr(in_3));  // open: en
  Register #(.width(32)) register_15 (.D(register_14_q), .Q(register_15_q), .clk(clock_1_out), .clr(in_3));  // open: en
  assign and_14_out = register_15_q & 32'h80;  // AND_Gate and_14, 32 bits wide
  assign and_15_out = register_16_q & 32'h58a0103a;  // AND_Gate and_15, 32 bits wide
  Register #(.width(32)) register_16 (.D(register_15_q), .Q(register_16_q), .clk(clock_1_out), .clr(in_3));  // open: en
  Register #(.width(32)) register_17 (.D(register_16_q), .Q(register_17_q), .clk(clock_1_out), .clr(in_3));  // open: en
  assign and_16_out = register_17_q & 32'h15504520;  // AND_Gate and_16, 32 bits wide
  assign and_17_out = register_18_q & 32'h8000000;  // AND_Gate and_17, 32 bits wide
  Register #(.width(32)) register_18 (.D(register_17_q), .Q(register_18_q), .clk(clock_1_out), .clr(in_3));  // open: en
  assign and_18_out = register_19_q & 32'h2550;  // AND_Gate and_18, 32 bits wide
  Register #(.width(32)) register_19 (.D(register_18_q), .Q(register_19_q), .clk(clock_1_out), .clr(in_3));  // open: en
  Register #(.width(32)) register_20 (.D(register_19_q), .Q(register_20_q), .clk(clock_1_out), .clr(in_3));  // open: en
  assign and_19_out = register_20_q & 32'h80300c00;  // AND_Gate and_19, 32 bits wide
  assign and_20_out = register_21_q & {32{1'b0}};  // AND_Gate and_20, 32 bits wide
  Register #(.width(32)) register_21 (.D(register_20_q), .Q(register_21_q), .clk(clock_1_out), .clr(in_3));  // open: en
  assign and_21_out = register_22_q & 32'h732262;  // AND_Gate and_21, 32 bits wide
  Register #(.width(32)) register_22 (.D(register_21_q), .Q(register_22_q), .clk(clock_1_out), .clr(in_3));  // open: en
  Register #(.width(32)) register_23 (.D(register_22_q), .Q(register_23_q), .clk(clock_1_out), .clr(in_3));  // open: en
  assign and_22_out = register_23_q & 32'h50740000;  // AND_Gate and_22, 32 bits wide
  assign and_23_out = register_24_q & 32'h61;  // AND_Gate and_23, 32 bits wide
  Register #(.width(32)) register_24 (.D(register_23_q), .Q(register_24_q), .clk(clock_1_out), .clr(in_3));  // open: en
  Register #(.width(32)) register_25 (.D(register_24_q), .Q(register_25_q), .clk(clock_1_out), .clr(in_3));  // open: en
  assign and_24_out = register_25_q & 32'h30606000;  // AND_Gate and_24, 32 bits wide
  assign and_25_out = register_26_q & 32'h83;  // AND_Gate and_25, 32 bits wide
  Register #(.width(32)) register_26 (.D(register_25_q), .Q(register_26_q), .clk(clock_1_out), .clr(in_3));  // open: en
  assign and_26_out = register_27_q & 32'h30316004;  // AND_Gate and_26, 32 bits wide
  Register #(.width(32)) register_27 (.D(register_26_q), .Q(register_27_q), .clk(clock_1_out), .clr(in_3));  // open: en
  Register #(.width(32)) register_28 (.D(register_27_q), .Q(register_28_q), .clk(clock_1_out), .clr(in_3));  // open: en
  assign and_27_out = register_28_q & 32'hffffff83;  // AND_Gate and_27, 32 bits wide
  assign and_28_out = register_29_q & 32'h743260ff;  // AND_Gate and_28, 32 bits wide
  Register #(.width(32)) register_29 (.D(register_28_q), .Q(register_29_q), .clk(clock_1_out), .clr(in_3));  // open: en
  assign and_29_out = register_30_q & 32'h57000000;  // AND_Gate and_29, 32 bits wide
  Register #(.width(32)) register_30 (.D(register_29_q), .Q(register_30_q), .clk(clock_1_out), .clr(in_3));  // open: en
  Register #(.width(32)) register_31 (.D(register_30_q), .Q(register_31_q), .clk(clock_1_out), .clr(in_3));  // open: en
  assign and_30_out = register_31_q & 32'h9058b0;  // AND_Gate and_30, 32 bits wide
  assign and_31_out = register_32_q & {32{1'b0}};  // AND_Gate and_31, 32 bits wide
  Register #(.width(32)) register_32 (.D(register_31_q), .Q(register_32_q), .clk(clock_1_out), .clr(in_3));  // open: en
  Register #(.width(32)) register_33 (.D(register_32_q), .Q(register_33_q), .clk(clock_1_out), .clr(in_3));  // open: en
  assign and_32_out = register_33_q & {32{1'b0}};  // AND_Gate and_32, 32 bits wide
  Register #(.width(32)) register_34 (.D(register_33_q), .clk(clock_1_out), .clr(in_3));  // open: en, Q
  assign out_17 = and_17_out | and_32_out | and_31_out | and_30_out | and_29_out | and_28_out | and_27_out | and_26_out | and_25_out | and_24_out | and_23_out | and_22_out | and_21_out | and_20_out | and_19_out | and_18_out | and_16_out | and_15_out | and_14_out | and_13_out | and_12_out | and_11_out | and_10_out | and_9_out | and_8_out | and_7_out | and_6_out | and_5_out | and_4_out | and_3_out | and_2_out | and_1_out;  // OR_Gate or_1, 32 bits wide
endmodule

module instr_valid (
  input  [3:0] in_1,
  output out_2
);

  wire comparator_1_eq, comparator_1_gt, comparator_2_eq, comparator_2_lt, or_1_out, or_2_out;

  Comparator #(.width(4), .mode("unsigned")) comparator_1 (
    .a(in_1), .b(4'b0000), .gt(comparator_1_gt), .eq(comparator_1_eq));  // open: lt
  Comparator #(.width(4), .mode("unsigned")) comparator_2 (
    .a(in_1), .b(4'b1101), .eq(comparator_2_eq), .lt(comparator_2_lt));  // open: gt
  or or_1 (or_1_out, comparator_1_gt, comparator_1_eq);
  or or_2 (or_2_out, comparator_2_eq, comparator_2_lt);
  and and_1 (out_2, or_1_out, or_2_out);
endmodule

module need_reg (
  input  [3:0] in_1,
  output out_2
);

  wire comparator_1_eq, comparator_2_eq, comparator_3_eq, comparator_4_eq, comparator_5_eq, comparator_6_eq,
       comparator_7_eq;

  Comparator #(.width(4), .mode("unsigned")) comparator_1 (
    .a(in_1), .b(4'b0010), .eq(comparator_1_eq));  // open: gt, lt
  Comparator #(.width(4), .mode("unsigned")) comparator_2 (
    .a(in_1), .b(4'b0110), .eq(comparator_2_eq));  // open: gt, lt
  Comparator #(.width(4), .mode("unsigned")) comparator_3 (
    .a(in_1), .b(4'b1010), .eq(comparator_3_eq));  // open: gt, lt
  Comparator #(.width(4), .mode("unsigned")) comparator_4 (
    .a(in_1), .b(4'b1011), .eq(comparator_4_eq));  // open: gt, lt
  Comparator #(.width(4), .mode("unsigned")) comparator_5 (
    .a(in_1), .b(4'b0011), .eq(comparator_5_eq));  // open: gt, lt
  Comparator #(.width(4), .mode("unsigned")) comparator_6 (
    .a(in_1), .b(4'b0100), .eq(comparator_6_eq));  // open: gt, lt
  Comparator #(.width(4), .mode("unsigned")) comparator_7 (
    .a(in_1), .b(4'b0101), .eq(comparator_7_eq));  // open: gt, lt
  or or_1 (out_2, comparator_1_eq, comparator_2_eq, comparator_3_eq, comparator_4_eq, comparator_5_eq, comparator_6_eq, comparator_7_eq);
endmodule

module need_valC (
  input  [3:0] in_1,
  output out_2
);

  wire comparator_1_eq, comparator_2_eq, comparator_3_eq, comparator_4_eq, comparator_5_eq;

  Comparator #(.width(4), .mode("unsigned")) comparator_1 (
    .a(in_1), .b(4'b0011), .eq(comparator_1_eq));  // open: gt, lt
  Comparator #(.width(4), .mode("unsigned")) comparator_2 (
    .a(in_1), .b(4'b0100), .eq(comparator_2_eq));  // open: gt, lt
  Comparator #(.width(4), .mode("unsigned")) comparator_3 (
    .a(in_1), .b(4'b0101), .eq(comparator_3_eq));  // open: gt, lt
  Comparator #(.width(4), .mode("unsigned")) comparator_4 (
    .a(in_1), .b(4'b0111), .eq(comparator_4_eq));  // open: gt, lt
  Comparator #(.width(4), .mode("unsigned")) comparator_5 (
    .a(in_1), .b(4'b1000), .eq(comparator_5_eq));  // open: gt, lt
  or or_1 (out_2, comparator_1_eq, comparator_2_eq, comparator_3_eq, comparator_4_eq, comparator_5_eq);
endmodule

module align (
  input  in_1,
  input  [3:0] in_2,
  input  [3:0] in_3,
  input  [31:0] in_4,
  output [3:0] out_5,
  output [3:0] out_6,
  output [31:0] out_7
);

  Multiplexer #(.width(4), .enable("false")) multiplexer_1 (.in1(in_2), .out(out_5), .sel(in_1));  // open: in0
  Multiplexer #(.width(4), .enable("false")) multiplexer_2 (.in1(in_3), .out(out_6), .sel(in_1));  // open: in0
  Multiplexer #(.width(32), .enable("false")) multiplexer_3 (
    .in0({in_2, in_3, in_4[31:8]}), .in1(in_4), .out(out_7), .sel(in_1));
endmodule

module instr_mem (
  input  in_1,
  input  in_2,
  input  in_3,
  input  [31:0] in_4,
  input  [31:0] in_5,
  input  [31:0] in_6,
  output [31:0] out_7,
  output [3:0] out_8,
  output [3:0] out_9,
  output [3:0] out_10,
  output [3:0] out_11
);

  wire demultiplexer_1_out0, demultiplexer_1_out1;
  wire [31:0] multiplexer_1_out;

  Demultiplexer #(.enable("false")) demultiplexer_1 (
    .out0(demultiplexer_1_out0), .out1(demultiplexer_1_out1), .in(1'b1), .sel(in_2));
  _32bit_RAM u_32bit_ram_1 (
    .in_5(in_1), .in_4(multiplexer_1_out), .in_1(demultiplexer_1_out0), .in_3(in_3), .in_6(in_6),
    .out_7({out_7[23:16], out_7[31:24], out_10, out_11, out_8, out_9}), .out_8({out_7[7:0], out_7[15:8]}),
    .in_2(demultiplexer_1_out1));
  Multiplexer #(.width(32), .enable("false")) multiplexer_1 (
    .in0(in_4), .in1(in_5), .out(multiplexer_1_out), .sel(in_2));
endmodule

module RegisterFile (
  input  [3:0] in_1,
  input  [31:0] in_2,
  input  [3:0] in_3,
  input  [3:0] in_4,
  input  in_5,
  input  [31:0] in_6,
  input  [3:0] in_7,
  input  in_8,
  output [31:0] out_9,
  output [31:0] out_10
);

  wire not_1_out, not_2_out, or_1_out, or_2_out, or_3_out, or_4_out, or_5_out, or_6_out, or_7_out, or_8_out;
  wire [7:0] and_3_out, and_4_out, decoder_1_out0, decoder_2_out0;
  wire [7:7] and_1_out, and_2_out;
  wire [31:0] multiplexer_1_out, multiplexer_2_out, multiplexer_3_out, multiplexer_4_out, multiplexer_5_out,
       multiplexer_6_out, multiplexer_7_out, multiplexer_8_out, register_1_q, register_2_q, register_3_q,
       register_4_q, register_5_q, register_6_q, register_7_q, register_8_q;

  Decoder #(.select(3), .enable("false")) decoder_1 (
    .out0(decoder_1_out0[0]), .out1(decoder_1_out0[1]), .out2(decoder_1_out0[2]), .out3(decoder_1_out0[3]),
    .out4(decoder_1_out0[4]), .out5(decoder_1_out0[5]), .out6(decoder_1_out0[6]), .out7(decoder_1_out0[7]),
    .sel(in_3[2:0]));
  Decoder #(.select(3), .enable("false")) decoder_2 (
    .out0(decoder_2_out0[0]), .out1(decoder_2_out0[1]), .out2(decoder_2_out0[2]), .out3(decoder_2_out0[3]),
    .out4(decoder_2_out0[4]), .out5(decoder_2_out0[5]), .out6(decoder_2_out0[6]), .out7(decoder_2_out0[7]),
    .sel(in_4[2:0]));
  not not_1 (not_1_out, in_3[3]);
  not not_2 (not_2_out, in_4[3]);
  and and_1 (and_1_out[7], not_1_out, 1'b1);
  and and_2 (and_2_out[7], not_2_out, 1'b1);
  assign and_3_out = {8{and_1_out[7]}} & decoder_1_out0;  // AND_Gate and_3, 8 bits wide
  assign and_4_out = decoder_2_out0 & {8{and_2_out[7]}};  // AND_Gate and_4, 8 bits wide
  Multiplexer #(.select(2), .width(32), .enable("false")) multiplexer_1 (
    .in0({32{1'b0}}), .in1(in_2), .in2(in_6), .out(multiplexer_1_out), .sel({and_4_out[0], and_3_out[0]}));  // open: in3
  Multiplexer #(.select(2), .width(32), .enable("false")) multiplexer_2 (
    .in0({32{1'b0}}), .in1(in_2), .in2(in_6), .out(multiplexer_2_out), .sel({and_4_out[1], and_3_out[1]}));  // open: in3
  Multiplexer #(.select(2), .width(32), .enable("false")) multiplexer_3 (
    .in0({32{1'b0}}), .in1(in_2), .in2(in_6), .out(multiplexer_3_out), .sel({and_4_out[2], and_3_out[2]}));  // open: in3
  Multiplexer #(.select(2), .width(32), .enable("false")) multiplexer_4 (
    .in0({32{1'b0}}), .in1(in_2), .in2(in_6), .out(multiplexer_4_out), .sel({and_4_out[3], and_3_out[3]}));  // open: in3
  Multiplexer #(.select(2), .width(32), .enable("false")) multiplexer_5 (
    .in0({32{1'b0}}), .in1(in_2), .in2(in_6), .out(multiplexer_5_out), .sel({and_4_out[4], and_3_out[4]}));  // open: in3
  Multiplexer #(.select(2), .width(32), .enable("false")) multiplexer_6 (
    .in0({32{1'b0}}), .in1(in_2), .in2(in_6), .out(multiplexer_6_out), .sel({and_4_out[5], and_3_out[5]}));  // open: in3
  Multiplexer #(.select(2), .width(32), .enable("false")) multiplexer_7 (
    .in0({32{1'b0}}), .in1(in_2), .in2(in_6), .out(multiplexer_7_out), .sel({and_4_out[6], and_3_out[6]}));  // open: in3
  Multiplexer #(.select(2), .width(32), .enable("false")) multiplexer_8 (
    .in0({32{1'b0}}), .in1(in_2), .in2(in_6), .out(multiplexer_8_out), .sel({and_4_out[7], and_3_out[7]}));  // open: in3
  or or_1 (or_1_out, and_3_out[0], and_4_out[0]);
  or or_2 (or_2_out, and_3_out[1], and_4_out[1]);
  or or_3 (or_3_out, and_3_out[2], and_4_out[2]);
  or or_4 (or_4_out, and_3_out[3], and_4_out[3]);
  or or_5 (or_5_out, and_3_out[4], and_4_out[4]);
  or or_6 (or_6_out, and_3_out[5], and_4_out[5]);
  or or_7 (or_7_out, and_3_out[6], and_4_out[6]);
  or or_8 (or_8_out, and_3_out[7], and_4_out[7]);
  Register #(.width(32)) register_1 (.D(multiplexer_1_out), .en(or_1_out), .Q(register_1_q), .clk(in_8), .clr(in_5));
  Register #(.width(32)) register_2 (.D(multiplexer_2_out), .en(or_2_out), .Q(register_2_q), .clk(in_8), .clr(in_5));
  Register #(.width(32)) register_3 (.D(multiplexer_3_out), .en(or_3_out), .Q(register_3_q), .clk(in_8), .clr(in_5));
  Register #(.width(32)) register_4 (.D(multiplexer_4_out), .en(or_4_out), .Q(register_4_q), .clk(in_8), .clr(in_5));
  Register #(.width(32)) register_5 (.D(multiplexer_5_out), .en(or_5_out), .Q(register_5_q), .clk(in_8), .clr(in_5));
  Register #(.width(32)) register_6 (.D(multiplexer_6_out), .en(or_6_out), .Q(register_6_q), .clk(in_8), .clr(in_5));
  Register #(.width(32)) register_7 (.D(multiplexer_7_out), .en(or_7_out), .Q(register_7_q), .clk(in_8), .clr(in_5));
  Register #(.width(32)) register_8 (.D(multiplexer_8_out), .en(or_8_out), .Q(register_8_q), .clk(in_8), .clr(in_5));
  Multiplexer #(.select(3), .width(32), .enable("false")) multiplexer_9 (
    .in0(register_1_q), .in1(register_2_q), .in2(register_3_q), .in3(register_4_q), .in4(register_5_q),
    .in5(register_6_q), .in6(register_7_q), .in7(register_8_q), .out(out_9), .sel(in_1[2:0]));
  Multiplexer #(.select(3), .width(32), .enable("false")) multiplexer_10 (
    .in0(register_1_q), .in1(register_2_q), .in2(register_3_q), .in3(register_4_q), .in4(register_5_q),
    .in5(register_6_q), .in6(register_7_q), .in7(register_8_q), .out(out_10), .sel(in_7[2:0]));
endmodule

module srcA (
  input  [3:0] in_1,
  input  [3:0] in_2,
  output [3:0] out_3
);

  wire comparator_1_eq, comparator_2_eq, comparator_3_eq, comparator_4_eq, comparator_5_eq, comparator_6_eq,
       or_1_out, or_2_out;
  wire [3:0] multiplexer_2_out;

  Comparator #(.width(4), .mode("unsigned")) comparator_1 (
    .a(in_2), .b(4'b1010), .eq(comparator_1_eq));  // open: gt, lt
  Comparator #(.width(4), .mode("unsigned")) comparator_2 (
    .a(in_2), .b(4'b0110), .eq(comparator_2_eq));  // open: gt, lt
  Comparator #(.width(4), .mode("unsigned")) comparator_3 (
    .a(in_2), .b(4'b0100), .eq(comparator_3_eq));  // open: gt, lt
  Comparator #(.width(4), .mode("unsigned")) comparator_4 (
    .a(in_2), .b(4'b0010), .eq(comparator_4_eq));  // open: gt, lt
  Comparator #(.width(4), .mode("unsigned")) comparator_5 (
    .a(in_2), .b(4'b1001), .eq(comparator_5_eq));  // open: gt, lt
  Comparator #(.width(4), .mode("unsigned")) comparator_6 (
    .a(in_2), .b(4'b1011), .eq(comparator_6_eq));  // open: gt, lt
  or or_1 (or_1_out, comparator_1_eq, comparator_2_eq, comparator_3_eq, comparator_4_eq);
  or or_2 (or_2_out, comparator_5_eq, comparator_6_eq);
  Multiplexer #(.width(4), .enable("false")) multiplexer_1 (
    .in0(multiplexer_2_out), .in1(in_1), .out(out_3), .sel(or_1_out));
  Multiplexer #(.width(4), .enable("false")) multiplexer_2 (
    .in0(4'b1111), .in1(4'b0100), .out(multiplexer_2_out), .sel(or_2_out));
endmodule

module srcB (
  input  [3:0] in_1,
  input  [3:0] in_2,
  output [3:0] out_3
);

  wire comparator_1_eq, comparator_2_eq, comparator_3_eq, comparator_4_eq, comparator_5_eq, comparator_6_eq,
       comparator_7_eq, or_1_out, or_2_out;
  wire [3:0] multiplexer_2_out;

  Comparator #(.width(4), .mode("unsigned")) comparator_1 (
    .a(in_2), .b(4'b0110), .eq(comparator_1_eq));  // open: gt, lt
  Comparator #(.width(4), .mode("unsigned")) comparator_2 (
    .a(in_2), .b(4'b0100), .eq(comparator_2_eq));  // open: gt, lt
  Comparator #(.width(4), .mode("unsigned")) comparator_3 (
    .a(in_2), .b(4'b0101), .eq(comparator_3_eq));  // open: gt, lt
  Comparator #(.width(4), .mode("unsigned")) comparator_4 (
    .a(in_2), .b(4'b1000), .eq(comparator_4_eq));  // open: gt, lt
  Comparator #(.width(4), .mode("unsigned")) comparator_5 (
    .a(in_2), .b(4'b1001), .eq(comparator_5_eq));  // open: gt, lt
  Comparator #(.width(4), .mode("unsigned")) comparator_6 (
    .a(in_2), .b(4'b1010), .eq(comparator_6_eq));  // open: gt, lt
  Comparator #(.width(4), .mode("unsigned")) comparator_7 (
    .a(in_2), .b(4'b1011), .eq(comparator_7_eq));  // open: gt, lt
  or or_1 (or_1_out, comparator_1_eq, comparator_2_eq, comparator_3_eq);
  or or_2 (or_2_out, comparator_4_eq, comparator_5_eq, comparator_6_eq, comparator_7_eq);
  Multiplexer #(.width(4), .enable("false")) multiplexer_1 (
    .in0(multiplexer_2_out), .in1(in_1), .out(out_3), .sel(or_1_out));
  Multiplexer #(.width(4), .enable("false")) multiplexer_2 (
    .in0(4'b1111), .in1(4'b0100), .out(multiplexer_2_out), .sel(or_2_out));
endmodule

module dstE (
  input  in_1,
  input  [3:0] in_2,
  input  [3:0] in_3,
  output [3:0] out_4
);

  wire and_1_out, comparator_1_eq, comparator_2_eq, comparator_3_eq, comparator_4_eq, comparator_5_eq,
       comparator_6_eq, comparator_7_eq, or_1_out, or_2_out;
  wire [3:0] multiplexer_2_out;

  Comparator #(.width(4), .mode("unsigned")) comparator_1 (
    .a(in_3), .b(4'b0010), .eq(comparator_1_eq));  // open: gt, lt
  Comparator #(.width(4), .mode("unsigned")) comparator_2 (
    .a(in_3), .b(4'b0011), .eq(comparator_2_eq));  // open: gt, lt
  Comparator #(.width(4), .mode("unsigned")) comparator_3 (
    .a(in_3), .b(4'b0110), .eq(comparator_3_eq));  // open: gt, lt
  Comparator #(.width(4), .mode("unsigned")) comparator_4 (
    .a(in_3), .b(4'b1000), .eq(comparator_4_eq));  // open: gt, lt
  Comparator #(.width(4), .mode("unsigned")) comparator_5 (
    .a(in_3), .b(4'b1001), .eq(comparator_5_eq));  // open: gt, lt
  Comparator #(.width(4), .mode("unsigned")) comparator_6 (
    .a(in_3), .b(4'b1010), .eq(comparator_6_eq));  // open: gt, lt
  Comparator #(.width(4), .mode("unsigned")) comparator_7 (
    .a(in_3), .b(4'b1011), .eq(comparator_7_eq));  // open: gt, lt
  and and_1 (and_1_out, in_1, comparator_1_eq);
  or or_1 (or_1_out, comparator_4_eq, comparator_5_eq, comparator_6_eq, comparator_7_eq);
  Multiplexer #(.width(4), .enable("false")) multiplexer_1 (
    .in0(multiplexer_2_out), .in1(in_2), .out(out_4), .sel(or_2_out));
  or or_2 (or_2_out, and_1_out, comparator_2_eq, comparator_3_eq);
  Multiplexer #(.width(4), .enable("false")) multiplexer_2 (
    .in0(4'b1111), .in1(4'b0100), .out(multiplexer_2_out), .sel(or_1_out));
endmodule

module dstM (
  input  [3:0] in_1,
  input  [3:0] in_2,
  output [3:0] out_3
);

  wire comparator_1_eq, comparator_2_eq, or_1_out;

  Comparator #(.width(4), .mode("unsigned")) comparator_1 (
    .a(in_2), .b(4'b0101), .eq(comparator_1_eq));  // open: gt, lt
  Comparator #(.width(4), .mode("unsigned")) comparator_2 (
    .a(in_2), .b(4'b1011), .eq(comparator_2_eq));  // open: gt, lt
  or or_1 (or_1_out, comparator_1_eq, comparator_2_eq);
  Multiplexer #(.width(4), .enable("false")) multiplexer_1 (.in0(4'b1111), .in1(in_1), .out(out_3), .sel(or_1_out));
endmodule

module ALU (
  input  [31:0] in_1,
  input  [31:0] in_2,
  input  in_3,
  input  in_4,
  input  in_5,
  input  in_6,
  output [31:0] out_7,
  output [2:0] out_8,
  output out_9
);

  wire and_1_out, and_2_out, and_3_out, and_4_out, and_5_out, and_6_out, and_7_out, and_8_out, and_9_out,
       and_10_out, and_11_out, and_12_out, and_13_out, and_14_out, and_15_out, and_16_out, multiplexer_3_out,
       not_1_out, not_2_out, not_3_out, not_4_out, or_1_out, or_5_out;
  wire [0:0] or_4_out;
  wire [1:0] or_2_out;
  wire [31:0] arithmeticunit_1_out_5, logicunit_1_out_4, multiplexer_1_out, n32bit_shifter_1_out_5;

  ArithmeticUnit arithmeticunit_1 (
    .out_7(out_8[1]), .out_9(out_9), .in_1(or_1_out), .in_2(or_2_out), .out_5(arithmeticunit_1_out_5),
    .in_3(in_1), .in_4(in_2), .out_8(out_8[2]), .out_6(out_8[0]));
  Multiplexer #(.width(32), .enable("false")) multiplexer_1 (
    .in0(arithmeticunit_1_out_5), .in1(logicunit_1_out_4), .out(multiplexer_1_out), .sel(or_4_out[0]));
  LogicUnit logicunit_1 (.in_1(or_2_out), .out_4(logicunit_1_out_4), .in_2(in_1), .in_3(in_2));
  not not_1 (not_1_out, in_5);
  not not_2 (not_2_out, in_4);
  not not_3 (not_3_out, in_3);
  Multiplexer #(.width(32), .enable("false")) multiplexer_2 (
    .in0(multiplexer_1_out), .in1(n32bit_shifter_1_out_5), .out(out_7), .sel(or_5_out));
  not not_4 (not_4_out, in_6);
  or or_1 (or_1_out, and_11_out, and_10_out, and_15_out);
  and and_1 (and_1_out, in_6, in_5, in_4, in_3);
  and and_2 (and_2_out, not_4_out, in_5, in_4, in_3);
  and and_3 (and_3_out, in_6, not_1_out, in_4, in_3);
  and and_4 (and_4_out, not_4_out, not_1_out, in_4, in_3);
  and and_5 (and_5_out, in_6, in_5, not_2_out, in_3);
  and and_6 (and_6_out, not_4_out, in_5, not_2_out, in_3);
  and and_7 (and_7_out, in_6, not_1_out, not_2_out, in_3);
  and and_8 (and_8_out, not_4_out, not_1_out, not_2_out, in_3);
  and and_9 (and_9_out, in_6, in_5, in_4, not_3_out);
  and and_10 (and_10_out, not_4_out, in_5, in_4, not_3_out);
  and and_11 (and_11_out, in_6, not_1_out, in_4, not_3_out);
  and and_12 (and_12_out, not_4_out, not_1_out, in_4, not_3_out);
  and and_13 (and_13_out, in_6, in_5, not_2_out, not_3_out);
  and and_14 (and_14_out, not_4_out, in_5, not_2_out, not_3_out);
  and and_15 (and_15_out, in_6, not_1_out, not_2_out, not_3_out);
  and and_16 (and_16_out, not_4_out, not_1_out, not_2_out, not_3_out);
  or or_2 (or_2_out[0], and_16_out, and_10_out, and_8_out, and_14_out, and_6_out, and_3_out);
  Multiplexer #(.enable("false")) multiplexer_3 (
    .in0(1'b0), .in1(in_2[31]), .out(multiplexer_3_out), .sel(or_2_out[0]));
  or or_3 (or_2_out[1], and_9_out, and_15_out, and_8_out, and_13_out, and_6_out, and_4_out, and_3_out);
  _32bit_Shifter u_32bit_shifter_1 (
    .in_2(multiplexer_3_out), .in_3(1'b0), .in_4({or_2_out[1], or_4_out[0]}), .in_1(in_2),
    .out_5(n32bit_shifter_1_out_5));
  or or_4 (or_4_out[0], and_7_out, and_14_out, and_13_out, and_6_out, and_2_out);
  or or_5 (or_5_out, and_2_out, and_3_out, and_4_out, and_5_out);
endmodule

module ArithmeticUnit (
  input  in_1,
  input  [1:0] in_2,
  input  [31:0] in_3,
  input  [31:0] in_4,
  output [31:0] out_5,
  output out_6,
  output out_7,
  output out_8,
  output out_9
);

  wire adder_1_cout;
  wire [30:0] multiplexer_1_out;
  wire [31:0] not_1_out;
  wire [31:31] multiplexer_1_out_2;

  Comparator #(.width(32)) comparator_1 (.a(out_5), .b({32{1'b0}}), .eq(out_6));  // open: gt, lt
  xor xor_1 (out_7, adder_1_cout, out_9);
  Adder #(.width(31)) adder_1 (
    .a(in_3[30:0]), .b(multiplexer_1_out), .out(out_5[30:0]), .cin(in_1), .cout(adder_1_cout));
  Adder #(.width(1)) adder_2 (
    .a(in_3[31]), .b(multiplexer_1_out_2[31]), .out(out_5[31]), .cin(adder_1_cout), .cout(out_9));
  Multiplexer #(.select(2), .width(32), .enable("false")) multiplexer_1 (
    .in0({32{1'b0}}), .in1(in_4), .in2(not_1_out), .in3({32{1'b1}}),
    .out({multiplexer_1_out_2[31], multiplexer_1_out}), .sel(in_2));
  assign not_1_out = ~in_4;  // NOT_Gate not_1, 32 bits wide

  assign out_8 = out_5[31];
endmodule

module LogicUnit (
  input  [1:0] in_1,
  input  [31:0] in_2,
  input  [31:0] in_3,
  output [31:0] out_4
);

  wire [31:0] and_1_out, not_1_out, or_1_out, xor_1_out;

  assign or_1_out = in_2 | in_3;  // OR_Gate or_1, 32 bits wide
  Multiplexer #(.select(2), .width(32), .enable("false")) multiplexer_1 (
    .in0(or_1_out), .in1(and_1_out), .in2(xor_1_out), .in3(not_1_out), .out(out_4), .sel(in_1));
  assign and_1_out = in_2 & in_3;  // AND_Gate and_1, 32 bits wide
  assign xor_1_out = in_2 ^ in_3;  // XOR_Gate xor_1, 32 bits wide
  assign not_1_out = ~in_2;  // NOT_Gate not_1, 32 bits wide
endmodule

module _4bit_Shifter (
  input  [3:0] in_1,
  input  in_2,
  input  in_3,
  input  [1:0] in_4,
  output [3:0] out_5
);

  Multiplexer #(.select(2), .enable("false")) multiplexer_1 (
    .in0(in_1[3]), .in1(in_1[2]), .in2(in_2), .in3(in_1[3]), .out(out_5[3]), .sel(in_4));
  Multiplexer #(.select(2), .enable("false")) multiplexer_2 (
    .in0(in_1[2]), .in1(in_1[1]), .in2(in_1[3]), .in3(in_1[2]), .out(out_5[2]), .sel(in_4));
  Multiplexer #(.select(2), .enable("false")) multiplexer_3 (
    .in0(in_1[1]), .in1(in_1[0]), .in2(in_1[2]), .in3(in_1[1]), .out(out_5[1]), .sel(in_4));
  Multiplexer #(.select(2), .enable("false")) multiplexer_4 (
    .in0(in_1[0]), .in1(in_3), .in2(in_1[1]), .in3(in_1[0]), .out(out_5[0]), .sel(in_4));
endmodule

module _8bit_Shifter (
  input  [7:0] in_1,
  input  in_2,
  input  in_3,
  input  [1:0] in_4,
  output [7:0] out_5
);

  _4bit_Shifter u_4bit_shifter_1 (.in_3(in_1[3]), .in_2(in_2), .in_4(in_4), .in_1(in_1[7:4]), .out_5(out_5[7:4]));
  _4bit_Shifter u_4bit_shifter_2 (.in_3(in_3), .in_2(in_1[4]), .in_4(in_4), .in_1(in_1[3:0]), .out_5(out_5[3:0]));
endmodule

module _16bit_Shifter (
  input  [15:0] in_1,
  input  in_2,
  input  in_3,
  input  [1:0] in_4,
  output [15:0] out_5
);

  _8bit_Shifter u_8bit_shifter_1 (.in_2(in_2), .in_3(in_1[7]), .in_4(in_4), .in_1(in_1[15:8]), .out_5(out_5[15:8]));
  _8bit_Shifter u_8bit_shifter_2 (.in_2(in_1[8]), .in_3(in_3), .in_4(in_4), .in_1(in_1[7:0]), .out_5(out_5[7:0]));
endmodule

module _32bit_Shifter (
  input  [31:0] in_1,
  input  in_2,
  input  in_3,
  input  [1:0] in_4,
  output [31:0] out_5
);

  _16bit_Shifter u_16bit_shifter_1 (
    .in_2(in_2), .in_3(in_1[15]), .in_4(in_4), .in_1(in_1[31:16]), .out_5(out_5[31:16]));
  _16bit_Shifter u_16bit_shifter_2 (.in_2(in_1[16]), .in_3(in_3), .in_4(in_4), .in_1(in_1[15:0]), .out_5(out_5[15:0]));
endmodule

module aluA (
  input  [31:0] in_1,
  input  [31:0] in_2,
  input  [3:0] in_3,
  output [31:0] out_4
);

  wire comparator_1_eq, comparator_2_eq, comparator_3_eq, comparator_4_eq, comparator_5_eq, comparator_6_eq,
       comparator_7_eq, comparator_8_eq, comparator_9_eq, or_1_out, or_2_out, or_3_out, or_4_out;
  wire [31:0] multiplexer_1_out, multiplexer_3_out, multiplexer_4_out, subtractor_1_out, undriven;

  Comparator #(.width(4), .mode("unsigned")) comparator_1 (
    .a(in_3), .b(4'b0010), .eq(comparator_1_eq));  // open: gt, lt
  Comparator #(.width(4), .mode("unsigned")) comparator_2 (
    .a(in_3), .b(4'b0110), .eq(comparator_2_eq));  // open: gt, lt
  Comparator #(.width(4), .mode("unsigned")) comparator_3 (
    .a(in_3), .b(4'b0011), .eq(comparator_3_eq));  // open: gt, lt
  Comparator #(.width(4), .mode("unsigned")) comparator_4 (
    .a(in_3), .b(4'b0100), .eq(comparator_4_eq));  // open: gt, lt
  Comparator #(.width(4), .mode("unsigned")) comparator_5 (
    .a(in_3), .b(4'b0101), .eq(comparator_5_eq));  // open: gt, lt
  Comparator #(.width(4), .mode("unsigned")) comparator_6 (
    .a(in_3), .b(4'b1000), .eq(comparator_6_eq));  // open: gt, lt
  Comparator #(.width(4), .mode("unsigned")) comparator_7 (
    .a(in_3), .b(4'b1010), .eq(comparator_7_eq));  // open: gt, lt
  Comparator #(.width(4), .mode("unsigned")) comparator_8 (
    .a(in_3), .b(4'b1001), .eq(comparator_8_eq));  // open: gt, lt
  Comparator #(.width(4), .mode("unsigned")) comparator_9 (
    .a(in_3), .b(4'b1011), .eq(comparator_9_eq));  // open: gt, lt
  or or_1 (or_1_out, comparator_1_eq, comparator_2_eq);
  or or_2 (or_2_out, comparator_3_eq, comparator_4_eq, comparator_5_eq);
  or or_3 (or_3_out, comparator_6_eq, comparator_7_eq);
  or or_4 (or_4_out, comparator_8_eq, comparator_9_eq);
  Multiplexer #(.width(32), .enable("false")) multiplexer_1 (
    .in0(undriven), .in1(32'h4), .out(multiplexer_1_out), .sel(or_4_out));
  Multiplexer #(.width(32), .enable("false")) multiplexer_2 (
    .in0(multiplexer_3_out), .in1(in_1), .out(out_4), .sel(or_1_out));
  Multiplexer #(.width(32), .enable("false")) multiplexer_3 (
    .in0(multiplexer_4_out), .in1(in_2), .out(multiplexer_3_out), .sel(or_2_out));
  Multiplexer #(.width(32), .enable("false")) multiplexer_4 (
    .in0(multiplexer_1_out), .in1(subtractor_1_out), .out(multiplexer_4_out), .sel(or_3_out));
  Subtractor #(.width(32)) subtractor_1 (.a({32{1'b0}}), .b(32'h4), .out(subtractor_1_out));  // open: bin, bout
endmodule

module aluB (
  input  [31:0] in_1,
  input  [3:0] in_2,
  output [31:0] out_3
);

  wire comparator_1_eq, comparator_2_eq, comparator_3_eq, comparator_4_eq, comparator_5_eq, comparator_6_eq,
       comparator_7_eq, comparator_8_eq, comparator_9_eq, or_1_out, or_2_out;
  wire [31:0] multiplexer_2_out, undriven;

  Comparator #(.width(4), .mode("unsigned")) comparator_1 (
    .a(in_2), .b(4'b0100), .eq(comparator_1_eq));  // open: gt, lt
  Comparator #(.width(4), .mode("unsigned")) comparator_2 (
    .a(in_2), .b(4'b0101), .eq(comparator_2_eq));  // open: gt, lt
  Comparator #(.width(4), .mode("unsigned")) comparator_3 (
    .a(in_2), .b(4'b0110), .eq(comparator_3_eq));  // open: gt, lt
  Comparator #(.width(4), .mode("unsigned")) comparator_4 (
    .a(in_2), .b(4'b1000), .eq(comparator_4_eq));  // open: gt, lt
  Comparator #(.width(4), .mode("unsigned")) comparator_5 (
    .a(in_2), .b(4'b1001), .eq(comparator_5_eq));  // open: gt, lt
  Comparator #(.width(4), .mode("unsigned")) comparator_6 (
    .a(in_2), .b(4'b1010), .eq(comparator_6_eq));  // open: gt, lt
  Comparator #(.width(4), .mode("unsigned")) comparator_7 (
    .a(in_2), .b(4'b1011), .eq(comparator_7_eq));  // open: gt, lt
  Comparator #(.width(4), .mode("unsigned")) comparator_8 (
    .a(in_2), .b(4'b0010), .eq(comparator_8_eq));  // open: gt, lt
  Comparator #(.width(4), .mode("unsigned")) comparator_9 (
    .a(in_2), .b(4'b0011), .eq(comparator_9_eq));  // open: gt, lt
  or or_1 (or_1_out, comparator_8_eq, comparator_9_eq);
  or or_2 (or_2_out, comparator_1_eq, comparator_2_eq, comparator_3_eq, comparator_4_eq, comparator_5_eq, comparator_6_eq, comparator_7_eq);
  Multiplexer #(.width(32), .enable("false")) multiplexer_1 (
    .in0(multiplexer_2_out), .in1(in_1), .out(out_3), .sel(or_2_out));
  Multiplexer #(.width(32), .enable("false")) multiplexer_2 (
    .in0(undriven), .in1({32{1'b0}}), .out(multiplexer_2_out), .sel(or_1_out));
endmodule

module alufun (
  input  [3:0] in_1,
  input  [3:0] in_2,
  output [3:0] out_3
);

  wire comparator_1_eq;

  Comparator #(.width(4), .mode("unsigned")) comparator_1 (
    .a(in_2), .b(4'b0110), .eq(comparator_1_eq));  // open: gt, lt
  Multiplexer #(.width(4), .enable("false")) multiplexer_1 (
    .in0(4'b0000), .in1(in_1), .out(out_3), .sel(comparator_1_eq));
endmodule

module set_cc (
  input  [3:0] in_1,
  output out_2
);

  Comparator #(.width(4), .mode("unsigned")) comparator_1 (.a(in_1), .b(4'b0110), .eq(out_2));  // open: gt, lt
endmodule

module cc (
  input  [2:0] in_1,
  input  in_2,
  input  in_3,
  output [2:0] out_4
);

  Register #(.width(3)) register_1 (.D(in_1), .en(in_2), .Q(out_4), .clk(in_3));  // open: clr
endmodule

module cond (
  input  [2:0] in_1,
  input  [3:0] in_2,
  output out_3
);

  wire and_1_out, and_2_out, and_3_out, and_4_out, and_5_out, and_6_out, and_7_out, comparator_1_eq,
       comparator_2_eq, comparator_3_eq, comparator_4_eq, comparator_5_eq, comparator_6_eq, comparator_7_eq,
       not_1_out, not_2_out, not_3_out, not_4_out, or_1_out, xor_1_out, xor_2_out;

  Comparator #(.width(4)) comparator_1 (.a(4'b0110), .b(in_2), .eq(comparator_1_eq));  // open: gt, lt
  Comparator #(.width(4)) comparator_2 (.a(4'b0101), .b(in_2), .eq(comparator_2_eq));  // open: gt, lt
  Comparator #(.width(4)) comparator_3 (.a(4'b0100), .b(in_2), .eq(comparator_3_eq));  // open: gt, lt
  Comparator #(.width(4)) comparator_4 (.a(4'b0011), .b(in_2), .eq(comparator_4_eq));  // open: gt, lt
  Comparator #(.width(4)) comparator_5 (.a(4'b0010), .b(in_2), .eq(comparator_5_eq));  // open: gt, lt
  Comparator #(.width(4)) comparator_6 (.a(4'b0001), .b(in_2), .eq(comparator_6_eq));  // open: gt, lt
  Comparator #(.width(4)) comparator_7 (.a(4'b0000), .b(in_2), .eq(comparator_7_eq));  // open: gt, lt
  not not_1 (not_1_out, in_1[0]);
  not not_2 (not_2_out, in_1[1]);
  not not_3 (not_3_out, in_1[2]);
  xor xor_1 (xor_1_out, not_2_out, not_3_out);
  xor xor_2 (xor_2_out, in_1[1], in_1[2]);
  and and_1 (and_1_out, not_1_out, xor_1_out);
  and and_2 (and_2_out, and_1_out, comparator_1_eq);
  and and_3 (and_3_out, xor_1_out, comparator_2_eq);
  not not_4 (not_4_out, in_1[0]);
  and and_4 (and_4_out, not_4_out, comparator_3_eq);
  and and_5 (and_5_out, in_1[0], comparator_4_eq);
  and and_6 (and_6_out, comparator_5_eq, xor_2_out);
  or or_1 (or_1_out, in_1[0], xor_2_out);
  and and_7 (and_7_out, or_1_out, comparator_6_eq);
  or or_2 (out_3, and_2_out, and_3_out, and_4_out, and_5_out, and_6_out, and_7_out, comparator_7_eq);
endmodule

module _27bit_RAM (
  input  [26:0] in_1,
  input  in_2,
  input  in_3,
  input  in_4,
  input  [31:0] in_5,
  output [15:0] out_6,
  output [31:0] out_7
);

  wire multiplexer_23_out, multiplexer_24_out, multiplexer_25_out, multiplexer_26_out, multiplexer_27_out,
       multiplexer_28_out, multiplexer_29_out, multiplexer_30_out, not_1_out, not_2_out, not_3_out,
       not_4_out, not_5_out, not_6_out, not_7_out, not_8_out, not_9_out;
  wire [2:0] subtractor_1_out;
  wire [7:0] controlled_buffer_1_out, controlled_buffer_3_out, controlled_buffer_5_out,
       controlled_buffer_7_out, controlled_buffer_9_out, controlled_buffer_11_out, controlled_buffer_13_out,
       controlled_buffer_15_out, multiplexer_15_out, multiplexer_16_out, multiplexer_17_out,
       multiplexer_18_out, multiplexer_19_out, multiplexer_20_out, multiplexer_21_out, multiplexer_22_out,
       ram_1_data, ram_2_data, ram_3_data, ram_4_data, ram_5_data, ram_6_data, ram_7_data, ram_8_data;
  wire [23:0] bit_extender_1_out, bit_extender_2_out, bit_extender_3_out, bit_extender_4_out,
       bit_extender_5_out, bit_extender_6_out, bit_extender_7_out, bit_extender_8_out;
  wire [26:0] adder_1_out, adder_2_out, adder_3_out, adder_4_out, adder_5_out, adder_6_out, adder_7_out,
       multiplexer_1_out, multiplexer_2_out, multiplexer_3_out, multiplexer_4_out, multiplexer_5_out,
       multiplexer_6_out, multiplexer_7_out, multiplexer_8_out, shifter_1_out, shifter_2_out, shifter_3_out,
       shifter_4_out, shifter_5_out, shifter_6_out, shifter_7_out, shifter_8_out;

  Adder #(.width(27)) adder_1 (.a(in_1), .b(27'h1), .out(adder_1_out), .cin(1'b0));  // open: cout
  Adder #(.width(27)) adder_2 (.a(adder_1_out), .b(27'h1), .out(adder_2_out), .cin(1'b0));  // open: cout
  Adder #(.width(27)) adder_3 (.a(adder_2_out), .b(27'h1), .out(adder_3_out), .cin(1'b0));  // open: cout
  Adder #(.width(27)) adder_4 (.a(adder_3_out), .b(27'h1), .out(adder_4_out), .cin(1'b0));  // open: cout
  Adder #(.width(27)) adder_5 (.a(adder_6_out), .b(27'h1), .out(adder_5_out), .cin(1'b0));  // open: cout
  Adder #(.width(27)) adder_6 (.a(adder_4_out), .b(27'h1), .out(adder_6_out), .cin(1'b0));  // open: cout
  Subtractor #(.width(3)) subtractor_1 (.a(3'b000), .b(in_1[2:0]), .out(subtractor_1_out));  // open: bin, bout
  Adder #(.width(27)) adder_7 (.a(adder_5_out), .b(27'h1), .out(adder_7_out), .cin(1'b0));  // open: cout
  Multiplexer #(.select(3), .width(27), .enable("false")) multiplexer_1 (
    .in0(in_1), .in1(adder_1_out), .in2(adder_2_out), .in3(adder_3_out), .in4(adder_4_out),
    .in5(adder_6_out), .in6(adder_5_out), .in7(adder_7_out), .out(multiplexer_1_out), .sel(subtractor_1_out));
  Multiplexer #(.select(3), .width(27), .enable("false")) multiplexer_2 (
    .in0(adder_1_out), .in1(adder_2_out), .in2(adder_3_out), .in3(adder_4_out), .in4(adder_6_out),
    .in5(adder_5_out), .in6(adder_7_out), .in7(in_1), .out(multiplexer_2_out), .sel(subtractor_1_out));
  Multiplexer #(.select(3), .width(27), .enable("false")) multiplexer_3 (
    .in0(adder_2_out), .in1(adder_3_out), .in2(adder_4_out), .in3(adder_6_out), .in4(adder_5_out),
    .in5(adder_7_out), .in6(in_1), .in7(adder_1_out), .out(multiplexer_3_out), .sel(subtractor_1_out));
  Multiplexer #(.select(3), .width(27), .enable("false")) multiplexer_4 (
    .in0(adder_3_out), .in1(adder_4_out), .in2(adder_6_out), .in3(adder_5_out), .in4(adder_7_out),
    .in5(in_1), .in6(adder_1_out), .in7(adder_2_out), .out(multiplexer_4_out), .sel(subtractor_1_out));
  Multiplexer #(.select(3), .width(27), .enable("false")) multiplexer_5 (
    .in0(adder_4_out), .in1(adder_6_out), .in2(adder_5_out), .in3(adder_7_out), .in4(in_1),
    .in5(adder_1_out), .in6(adder_2_out), .in7(adder_3_out), .out(multiplexer_5_out), .sel(subtractor_1_out));
  Multiplexer #(.select(3), .width(27), .enable("false")) multiplexer_6 (
    .in0(adder_6_out), .in1(adder_5_out), .in2(adder_7_out), .in3(in_1), .in4(adder_1_out),
    .in5(adder_2_out), .in6(adder_3_out), .in7(adder_4_out), .out(multiplexer_6_out), .sel(subtractor_1_out));
  Multiplexer #(.select(3), .width(27), .enable("false")) multiplexer_7 (
    .in0(adder_5_out), .in1(adder_7_out), .in2(in_1), .in3(adder_1_out), .in4(adder_2_out),
    .in5(adder_3_out), .in6(adder_4_out), .in7(adder_6_out), .out(multiplexer_7_out), .sel(subtractor_1_out));
  Multiplexer #(.select(3), .width(27), .enable("false")) multiplexer_8 (
    .in0(adder_7_out), .in1(in_1), .in2(adder_1_out), .in3(adder_2_out), .in4(adder_3_out),
    .in5(adder_4_out), .in6(adder_6_out), .in7(adder_5_out), .out(multiplexer_8_out), .sel(subtractor_1_out));
  Shifter #(.width(27), .shift("lr")) shifter_1 (.in(multiplexer_1_out), .\dist (5'b00011), .out(shifter_1_out));
  Bit_Extender #(.in_width(27), .out_width(24)) bit_extender_1 (.in(shifter_1_out), .out(bit_extender_1_out));
  Shifter #(.width(27), .shift("lr")) shifter_2 (.in(multiplexer_2_out), .\dist (5'b00011), .out(shifter_2_out));
  Bit_Extender #(.in_width(27), .out_width(24)) bit_extender_2 (.in(shifter_2_out), .out(bit_extender_2_out));
  Shifter #(.width(27), .shift("lr")) shifter_3 (.in(multiplexer_3_out), .\dist (5'b00011), .out(shifter_3_out));
  Bit_Extender #(.in_width(27), .out_width(24)) bit_extender_3 (.in(shifter_3_out), .out(bit_extender_3_out));
  Bit_Extender #(.in_width(27), .out_width(24)) bit_extender_4 (.in(shifter_4_out), .out(bit_extender_4_out));
  Shifter #(.width(27), .shift("lr")) shifter_4 (.in(multiplexer_4_out), .\dist (5'b00011), .out(shifter_4_out));
  Shifter #(.width(27), .shift("lr")) shifter_5 (.in(multiplexer_5_out), .\dist (5'b00011), .out(shifter_5_out));
  Bit_Extender #(.in_width(27), .out_width(24)) bit_extender_5 (.in(shifter_5_out), .out(bit_extender_5_out));
  Bit_Extender #(.in_width(27), .out_width(24)) bit_extender_6 (.in(shifter_6_out), .out(bit_extender_6_out));
  Shifter #(.width(27), .shift("lr")) shifter_6 (.in(multiplexer_6_out), .\dist (5'b00011), .out(shifter_6_out));
  Shifter #(.width(27), .shift("lr")) shifter_7 (.in(multiplexer_7_out), .\dist (5'b00011), .out(shifter_7_out));
  Bit_Extender #(.in_width(27), .out_width(24)) bit_extender_7 (.in(shifter_7_out), .out(bit_extender_7_out));
  Bit_Extender #(.in_width(27), .out_width(24)) bit_extender_8 (.in(shifter_8_out), .out(bit_extender_8_out));
  Shifter #(.width(27), .shift("lr")) shifter_8 (.in(multiplexer_8_out), .\dist (5'b00011), .out(shifter_8_out));
  RAM #(.addrWidth(24)) ram_1 (
    .addr(bit_extender_1_out), .data(ram_1_data), .clk(in_3), .ld(multiplexer_23_out), .clr(in_2));  // open: sel
  not not_1 (not_1_out, multiplexer_23_out);
  RAM #(.addrWidth(24)) ram_2 (
    .addr(bit_extender_2_out), .data(ram_2_data), .clk(in_3), .ld(multiplexer_24_out), .clr(in_2));  // open: sel
  not not_2 (not_2_out, multiplexer_24_out);
  RAM #(.addrWidth(24)) ram_3 (
    .addr(bit_extender_3_out), .data(ram_3_data), .clk(in_3), .ld(multiplexer_25_out), .clr(in_2));  // open: sel
  not not_3 (not_3_out, multiplexer_25_out);
  RAM #(.addrWidth(24)) ram_4 (
    .addr(bit_extender_4_out), .data(ram_4_data), .clk(in_3), .ld(multiplexer_26_out), .clr(in_2));  // open: sel
  not not_4 (not_4_out, multiplexer_26_out);
  RAM #(.addrWidth(24)) ram_5 (
    .addr(bit_extender_5_out), .data(ram_5_data), .clk(in_3), .ld(multiplexer_27_out), .clr(in_2));  // open: sel
  not not_5 (not_5_out, multiplexer_27_out);
  RAM #(.addrWidth(24)) ram_6 (
    .addr(bit_extender_6_out), .data(ram_6_data), .clk(in_3), .ld(multiplexer_28_out), .clr(in_2));  // open: sel
  not not_6 (not_6_out, multiplexer_28_out);
  RAM #(.addrWidth(24)) ram_7 (
    .addr(bit_extender_7_out), .data(ram_7_data), .clk(in_3), .ld(multiplexer_29_out), .clr(in_2));  // open: sel
  not not_7 (not_7_out, multiplexer_29_out);
  RAM #(.addrWidth(24)) ram_8 (
    .addr(bit_extender_8_out), .data(ram_8_data), .clk(in_3), .ld(multiplexer_30_out), .clr(in_2));  // open: sel
  not not_8 (not_8_out, multiplexer_30_out);
  assign controlled_buffer_1_out = multiplexer_23_out ? ram_1_data : 8'bz;  // Controlled_Buffer controlled_buffer_1
  assign ram_1_data = not_1_out ? multiplexer_15_out : 8'bz;  // Controlled_Buffer controlled_buffer_2
  assign controlled_buffer_3_out = multiplexer_24_out ? ram_2_data : 8'bz;  // Controlled_Buffer controlled_buffer_3
  assign ram_2_data = not_2_out ? multiplexer_16_out : 8'bz;  // Controlled_Buffer controlled_buffer_4
  assign controlled_buffer_5_out = multiplexer_25_out ? ram_3_data : 8'bz;  // Controlled_Buffer controlled_buffer_5
  assign ram_3_data = not_3_out ? multiplexer_17_out : 8'bz;  // Controlled_Buffer controlled_buffer_6
  assign controlled_buffer_7_out = multiplexer_26_out ? ram_4_data : 8'bz;  // Controlled_Buffer controlled_buffer_7
  assign ram_4_data = not_4_out ? multiplexer_18_out : 8'bz;  // Controlled_Buffer controlled_buffer_8
  assign controlled_buffer_9_out = multiplexer_27_out ? ram_5_data : 8'bz;  // Controlled_Buffer controlled_buffer_9
  assign ram_5_data = not_5_out ? multiplexer_19_out : 8'bz;  // Controlled_Buffer controlled_buffer_10
  assign controlled_buffer_11_out = multiplexer_28_out ? ram_6_data : 8'bz;  // Controlled_Buffer controlled_buffer_11
  assign ram_6_data = not_6_out ? multiplexer_20_out : 8'bz;  // Controlled_Buffer controlled_buffer_12
  assign controlled_buffer_13_out = multiplexer_29_out ? ram_7_data : 8'bz;  // Controlled_Buffer controlled_buffer_13
  assign ram_7_data = not_7_out ? multiplexer_21_out : 8'bz;  // Controlled_Buffer controlled_buffer_14
  assign controlled_buffer_15_out = multiplexer_30_out ? ram_8_data : 8'bz;  // Controlled_Buffer controlled_buffer_15
  assign ram_8_data = not_8_out ? multiplexer_22_out : 8'bz;  // Controlled_Buffer controlled_buffer_16
  Multiplexer #(.select(3), .width(8), .enable("false")) multiplexer_9 (
    .in0(controlled_buffer_1_out), .in1(controlled_buffer_3_out), .in2(controlled_buffer_5_out),
    .in3(controlled_buffer_7_out), .in4(controlled_buffer_9_out), .in5(controlled_buffer_11_out),
    .in6(controlled_buffer_13_out), .in7(controlled_buffer_15_out), .out(out_7[7:0]), .sel(in_1[2:0]));
  Multiplexer #(.select(3), .width(8), .enable("false")) multiplexer_10 (
    .in0(controlled_buffer_3_out), .in1(controlled_buffer_5_out), .in2(controlled_buffer_7_out),
    .in3(controlled_buffer_9_out), .in4(controlled_buffer_11_out), .in5(controlled_buffer_13_out),
    .in6(controlled_buffer_15_out), .in7(controlled_buffer_1_out), .out(out_7[15:8]), .sel(in_1[2:0]));
  Multiplexer #(.select(3), .width(8), .enable("false")) multiplexer_11 (
    .in0(controlled_buffer_5_out), .in1(controlled_buffer_7_out), .in2(controlled_buffer_9_out),
    .in3(controlled_buffer_11_out), .in4(controlled_buffer_13_out), .in5(controlled_buffer_15_out),
    .in6(controlled_buffer_1_out), .in7(controlled_buffer_3_out), .out(out_7[23:16]), .sel(in_1[2:0]));
  Multiplexer #(.select(3), .width(8), .enable("false")) multiplexer_12 (
    .in0(controlled_buffer_7_out), .in1(controlled_buffer_9_out), .in2(controlled_buffer_11_out),
    .in3(controlled_buffer_13_out), .in4(controlled_buffer_15_out), .in5(controlled_buffer_1_out),
    .in6(controlled_buffer_3_out), .in7(controlled_buffer_5_out), .out(out_7[31:24]), .sel(in_1[2:0]));
  Multiplexer #(.select(3), .width(8), .enable("false")) multiplexer_13 (
    .in0(controlled_buffer_9_out), .in1(controlled_buffer_11_out), .in2(controlled_buffer_13_out),
    .in3(controlled_buffer_15_out), .in4(controlled_buffer_1_out), .in5(controlled_buffer_3_out),
    .in6(controlled_buffer_5_out), .in7(controlled_buffer_7_out), .out(out_6[7:0]), .sel(in_1[2:0]));
  Multiplexer #(.select(3), .width(8), .enable("false")) multiplexer_14 (
    .in0(controlled_buffer_11_out), .in1(controlled_buffer_13_out), .in2(controlled_buffer_15_out),
    .in3(controlled_buffer_1_out), .in4(controlled_buffer_3_out), .in5(controlled_buffer_5_out),
    .in6(controlled_buffer_7_out), .in7(controlled_buffer_9_out), .out(out_6[15:8]), .sel(in_1[2:0]));
  Multiplexer #(.select(3), .width(8), .enable("false")) multiplexer_15 (
    .in0(in_5[7:0]), .in1({8{1'b0}}), .in2({8{1'b0}}), .in3({8{1'b0}}), .in4({8{1'b0}}), .in5(in_5[31:24]),
    .in6(in_5[23:16]), .in7(in_5[15:8]), .out(multiplexer_15_out), .sel(in_1[2:0]));
  Multiplexer #(.select(3), .width(8), .enable("false")) multiplexer_16 (
    .in0(in_5[15:8]), .in1(in_5[7:0]), .in2({8{1'b0}}), .in3({8{1'b0}}), .in4({8{1'b0}}), .in5({8{1'b0}}),
    .in6(in_5[31:24]), .in7(in_5[23:16]), .out(multiplexer_16_out), .sel(in_1[2:0]));
  Multiplexer #(.select(3), .width(8), .enable("false")) multiplexer_17 (
    .in0(in_5[23:16]), .in1(in_5[15:8]), .in2(in_5[7:0]), .in3({8{1'b0}}), .in4({8{1'b0}}), .in5({8{1'b0}}),
    .in6({8{1'b0}}), .in7(in_5[31:24]), .out(multiplexer_17_out), .sel(in_1[2:0]));
  Multiplexer #(.select(3), .width(8), .enable("false")) multiplexer_18 (
    .in0(in_5[31:24]), .in1(in_5[23:16]), .in2(in_5[15:8]), .in3(in_5[7:0]), .in4({8{1'b0}}),
    .in5({8{1'b0}}), .in6({8{1'b0}}), .in7({8{1'b0}}), .out(multiplexer_18_out), .sel(in_1[2:0]));
  Multiplexer #(.select(3), .width(8), .enable("false")) multiplexer_19 (
    .in0({8{1'b0}}), .in1(in_5[31:24]), .in2(in_5[23:16]), .in3(in_5[15:8]), .in4(in_5[7:0]),
    .in5({8{1'b0}}), .in6({8{1'b0}}), .in7({8{1'b0}}), .out(multiplexer_19_out), .sel(in_1[2:0]));
  Multiplexer #(.select(3), .width(8), .enable("false")) multiplexer_20 (
    .in0({8{1'b0}}), .in1({8{1'b0}}), .in2(in_5[31:24]), .in3(in_5[23:16]), .in4(in_5[15:8]),
    .in5(in_5[7:0]), .in6({8{1'b0}}), .in7({8{1'b0}}), .out(multiplexer_20_out), .sel(in_1[2:0]));
  Multiplexer #(.select(3), .width(8), .enable("false")) multiplexer_21 (
    .in0({8{1'b0}}), .in1({8{1'b0}}), .in2({8{1'b0}}), .in3(in_5[31:24]), .in4(in_5[23:16]),
    .in5(in_5[15:8]), .in6(in_5[7:0]), .in7({8{1'b0}}), .out(multiplexer_21_out), .sel(in_1[2:0]));
  Multiplexer #(.select(3), .width(8), .enable("false")) multiplexer_22 (
    .in0({8{1'b0}}), .in1({8{1'b0}}), .in2({8{1'b0}}), .in3({8{1'b0}}), .in4(in_5[31:24]), .in5(in_5[23:16]),
    .in6(in_5[15:8]), .in7(in_5[7:0]), .out(multiplexer_22_out), .sel(in_1[2:0]));
  Multiplexer #(.select(3), .enable("false")) multiplexer_23 (
    .in0(not_9_out), .in1(1'b1), .in2(1'b1), .in3(1'b1), .in4(1'b1), .in5(not_9_out), .in6(not_9_out),
    .in7(not_9_out), .out(multiplexer_23_out), .sel(in_1[2:0]));
  Multiplexer #(.select(3), .enable("false")) multiplexer_24 (
    .in0(not_9_out), .in1(not_9_out), .in2(1'b1), .in3(1'b1), .in4(1'b1), .in5(1'b1), .in6(not_9_out),
    .in7(not_9_out), .out(multiplexer_24_out), .sel(in_1[2:0]));
  Multiplexer #(.select(3), .enable("false")) multiplexer_25 (
    .in0(not_9_out), .in1(not_9_out), .in2(not_9_out), .in3(1'b1), .in4(1'b1), .in5(1'b1), .in6(1'b1),
    .in7(not_9_out), .out(multiplexer_25_out), .sel(in_1[2:0]));
  Multiplexer #(.select(3), .enable("false")) multiplexer_26 (
    .in0(not_9_out), .in1(not_9_out), .in2(not_9_out), .in3(not_9_out), .in4(1'b1), .in5(1'b1), .in6(1'b1),
    .in7(1'b1), .out(multiplexer_26_out), .sel(in_1[2:0]));
  Multiplexer #(.select(3), .enable("false")) multiplexer_27 (
    .in0(1'b1), .in1(not_9_out), .in2(not_9_out), .in3(not_9_out), .in4(not_9_out), .in5(1'b1), .in6(1'b1),
    .in7(1'b1), .out(multiplexer_27_out), .sel(in_1[2:0]));
  Multiplexer #(.select(3), .enable("false")) multiplexer_28 (
    .in0(1'b1), .in1(1'b1), .in2(not_9_out), .in3(not_9_out), .in4(not_9_out), .in5(not_9_out), .in6(1'b1),
    .in7(1'b1), .out(multiplexer_28_out), .sel(in_1[2:0]));
  Multiplexer #(.select(3), .enable("false")) multiplexer_29 (
    .in0(1'b1), .in1(1'b1), .in2(1'b1), .in3(not_9_out), .in4(not_9_out), .in5(not_9_out), .in6(not_9_out),
    .in7(1'b1), .out(multiplexer_29_out), .sel(in_1[2:0]));
  Multiplexer #(.select(3), .enable("false")) multiplexer_30 (
    .in0(1'b1), .in1(1'b1), .in2(1'b1), .in3(1'b1), .in4(not_9_out), .in5(not_9_out), .in6(not_9_out),
    .in7(not_9_out), .out(multiplexer_30_out), .sel(in_1[2:0]));
  not not_9 (not_9_out, in_4);
endmodule

module _32bit_RAM (
  input  in_1,
  input  in_2,
  input  in_3,
  input  [31:0] in_4,
  input  in_5,
  input  [31:0] in_6,
  output [31:0] out_7,
  output [15:0] out_8
);

  wire multiplexer_1_out;
  wire [15:0] n27bit_ram_1_out_6, n27bit_ram_2_out_6, n27bit_ram_3_out_6, n27bit_ram_4_out_6,
       n27bit_ram_5_out_6, n27bit_ram_6_out_6, n27bit_ram_7_out_6, n27bit_ram_8_out_6, n27bit_ram_9_out_6,
       n27bit_ram_10_out_6, n27bit_ram_11_out_6, n27bit_ram_12_out_6, n27bit_ram_13_out_6,
       n27bit_ram_14_out_6, n27bit_ram_15_out_6, n27bit_ram_16_out_6, n27bit_ram_17_out_6,
       n27bit_ram_18_out_6, n27bit_ram_19_out_6, n27bit_ram_20_out_6, n27bit_ram_21_out_6,
       n27bit_ram_22_out_6, n27bit_ram_23_out_6, n27bit_ram_24_out_6, n27bit_ram_25_out_6,
       n27bit_ram_26_out_6, n27bit_ram_27_out_6, n27bit_ram_28_out_6, n27bit_ram_29_out_6,
       n27bit_ram_30_out_6, n27bit_ram_31_out_6, n27bit_ram_32_out_6;
  wire [31:0] and_1_out, bit_extender_1_out, bit_extender_2_out, decoder_1_out0, n27bit_ram_1_out_7,
       n27bit_ram_2_out_7, n27bit_ram_3_out_7, n27bit_ram_4_out_7, n27bit_ram_5_out_7, n27bit_ram_6_out_7,
       n27bit_ram_7_out_7, n27bit_ram_8_out_7, n27bit_ram_9_out_7, n27bit_ram_10_out_7, n27bit_ram_11_out_7,
       n27bit_ram_12_out_7, n27bit_ram_13_out_7, n27bit_ram_14_out_7, n27bit_ram_15_out_7,
       n27bit_ram_16_out_7, n27bit_ram_17_out_7, n27bit_ram_18_out_7, n27bit_ram_19_out_7,
       n27bit_ram_20_out_7, n27bit_ram_21_out_7, n27bit_ram_22_out_7, n27bit_ram_23_out_7,
       n27bit_ram_24_out_7, n27bit_ram_25_out_7, n27bit_ram_26_out_7, n27bit_ram_27_out_7,
       n27bit_ram_28_out_7, n27bit_ram_29_out_7, n27bit_ram_30_out_7, n27bit_ram_31_out_7,
       n27bit_ram_32_out_7;

  _27bit_RAM u_27bit_ram_1 (
    .in_1(in_4[26:0]), .in_2(bit_extender_2_out[31]), .in_4(and_1_out[31]), .out_7(n27bit_ram_1_out_7),
    .out_6(n27bit_ram_1_out_6), .in_5(in_6), .in_3(in_5));
  _27bit_RAM u_27bit_ram_2 (
    .in_1(in_4[26:0]), .in_2(bit_extender_2_out[30]), .in_4(and_1_out[30]), .out_7(n27bit_ram_2_out_7),
    .out_6(n27bit_ram_2_out_6), .in_5(in_6), .in_3(in_5));
  _27bit_RAM u_27bit_ram_3 (
    .in_1(in_4[26:0]), .in_2(bit_extender_2_out[29]), .in_4(and_1_out[29]), .out_7(n27bit_ram_3_out_7),
    .out_6(n27bit_ram_3_out_6), .in_5(in_6), .in_3(in_5));
  _27bit_RAM u_27bit_ram_4 (
    .in_1(in_4[26:0]), .in_2(bit_extender_2_out[28]), .in_4(and_1_out[28]), .out_7(n27bit_ram_4_out_7),
    .out_6(n27bit_ram_4_out_6), .in_5(in_6), .in_3(in_5));
  Decoder #(.select(5), .enable("false")) decoder_1 (
    .out0(decoder_1_out0[0]), .out1(decoder_1_out0[1]), .out2(decoder_1_out0[2]), .out3(decoder_1_out0[3]),
    .out4(decoder_1_out0[4]), .out5(decoder_1_out0[5]), .out6(decoder_1_out0[6]), .out7(decoder_1_out0[7]),
    .out8(decoder_1_out0[8]), .out9(decoder_1_out0[9]), .out10(decoder_1_out0[10]),
    .out11(decoder_1_out0[11]), .out12(decoder_1_out0[12]), .out13(decoder_1_out0[13]),
    .out14(decoder_1_out0[14]), .out15(decoder_1_out0[15]), .out16(decoder_1_out0[16]),
    .out17(decoder_1_out0[17]), .out18(decoder_1_out0[18]), .out19(decoder_1_out0[19]),
    .out20(decoder_1_out0[20]), .out21(decoder_1_out0[21]), .out22(decoder_1_out0[22]),
    .out23(decoder_1_out0[23]), .out24(decoder_1_out0[24]), .out25(decoder_1_out0[25]),
    .out26(decoder_1_out0[26]), .out27(decoder_1_out0[27]), .out28(decoder_1_out0[28]),
    .out29(decoder_1_out0[29]), .out30(decoder_1_out0[30]), .out31(decoder_1_out0[31]), .sel(in_4[31:27]));
  _27bit_RAM u_27bit_ram_5 (
    .in_1(in_4[26:0]), .in_2(bit_extender_2_out[27]), .in_4(and_1_out[27]), .out_7(n27bit_ram_5_out_7),
    .out_6(n27bit_ram_5_out_6), .in_5(in_6), .in_3(in_5));
  _27bit_RAM u_27bit_ram_6 (
    .in_1(in_4[26:0]), .in_2(bit_extender_2_out[26]), .in_4(and_1_out[26]), .out_7(n27bit_ram_6_out_7),
    .out_6(n27bit_ram_6_out_6), .in_5(in_6), .in_3(in_5));
  _27bit_RAM u_27bit_ram_7 (
    .in_1(in_4[26:0]), .in_2(bit_extender_2_out[25]), .in_4(and_1_out[25]), .out_7(n27bit_ram_7_out_7),
    .out_6(n27bit_ram_7_out_6), .in_5(in_6), .in_3(in_5));
  _27bit_RAM u_27bit_ram_8 (
    .in_1(in_4[26:0]), .in_2(bit_extender_2_out[24]), .in_4(and_1_out[24]), .out_7(n27bit_ram_8_out_7),
    .out_6(n27bit_ram_8_out_6), .in_5(in_6), .in_3(in_5));
  Multiplexer #(.select(2), .enable("false")) multiplexer_1 (
    .in1(1'b1), .in2(1'b0), .out(multiplexer_1_out), .sel({in_1, in_2}));  // open: in0, in3
  assign and_1_out = decoder_1_out0 & bit_extender_1_out;  // AND_Gate and_1, 32 bits wide
  _27bit_RAM u_27bit_ram_9 (
    .in_1(in_4[26:0]), .in_2(bit_extender_2_out[23]), .in_4(and_1_out[23]), .out_7(n27bit_ram_9_out_7),
    .out_6(n27bit_ram_9_out_6), .in_5(in_6), .in_3(in_5));
  _27bit_RAM u_27bit_ram_10 (
    .in_1(in_4[26:0]), .in_2(bit_extender_2_out[22]), .in_4(and_1_out[22]), .out_7(n27bit_ram_10_out_7),
    .out_6(n27bit_ram_10_out_6), .in_5(in_6), .in_3(in_5));
  assign bit_extender_1_out = {{31{multiplexer_1_out}}, multiplexer_1_out};  // Bit_Extender bit_extender_1
  _27bit_RAM u_27bit_ram_11 (
    .in_1(in_4[26:0]), .in_2(bit_extender_2_out[21]), .in_4(and_1_out[21]), .out_7(n27bit_ram_11_out_7),
    .out_6(n27bit_ram_11_out_6), .in_5(in_6), .in_3(in_5));
  _27bit_RAM u_27bit_ram_12 (
    .in_1(in_4[26:0]), .in_2(bit_extender_2_out[20]), .in_4(and_1_out[20]), .out_7(n27bit_ram_12_out_7),
    .out_6(n27bit_ram_12_out_6), .in_5(in_6), .in_3(in_5));
  assign bit_extender_2_out = {{31{in_3}}, in_3};  // Bit_Extender bit_extender_2
  _27bit_RAM u_27bit_ram_13 (
    .in_1(in_4[26:0]), .in_2(bit_extender_2_out[19]), .in_4(and_1_out[19]), .out_7(n27bit_ram_13_out_7),
    .out_6(n27bit_ram_13_out_6), .in_5(in_6), .in_3(in_5));
  _27bit_RAM u_27bit_ram_14 (
    .in_1(in_4[26:0]), .in_2(bit_extender_2_out[18]), .in_4(and_1_out[18]), .out_7(n27bit_ram_14_out_7),
    .out_6(n27bit_ram_14_out_6), .in_5(in_6), .in_3(in_5));
  _27bit_RAM u_27bit_ram_15 (
    .in_1(in_4[26:0]), .in_2(bit_extender_2_out[17]), .in_4(and_1_out[17]), .out_7(n27bit_ram_15_out_7),
    .out_6(n27bit_ram_15_out_6), .in_5(in_6), .in_3(in_5));
  _27bit_RAM u_27bit_ram_16 (
    .in_1(in_4[26:0]), .in_2(bit_extender_2_out[16]), .in_4(and_1_out[16]), .out_7(n27bit_ram_16_out_7),
    .out_6(n27bit_ram_16_out_6), .in_5(in_6), .in_3(in_5));
  _27bit_RAM u_27bit_ram_17 (
    .in_1(in_4[26:0]), .in_2(bit_extender_2_out[15]), .in_4(and_1_out[15]), .out_7(n27bit_ram_17_out_7),
    .out_6(n27bit_ram_17_out_6), .in_5(in_6), .in_3(in_5));
  _27bit_RAM u_27bit_ram_18 (
    .in_1(in_4[26:0]), .in_2(bit_extender_2_out[14]), .in_4(and_1_out[14]), .out_7(n27bit_ram_18_out_7),
    .out_6(n27bit_ram_18_out_6), .in_5(in_6), .in_3(in_5));
  _27bit_RAM u_27bit_ram_19 (
    .in_1(in_4[26:0]), .in_2(bit_extender_2_out[13]), .in_4(and_1_out[13]), .out_7(n27bit_ram_19_out_7),
    .out_6(n27bit_ram_19_out_6), .in_5(in_6), .in_3(in_5));
  _27bit_RAM u_27bit_ram_20 (
    .in_1(in_4[26:0]), .in_2(bit_extender_2_out[12]), .in_4(and_1_out[12]), .out_7(n27bit_ram_20_out_7),
    .out_6(n27bit_ram_20_out_6), .in_5(in_6), .in_3(in_5));
  _27bit_RAM u_27bit_ram_21 (
    .in_1(in_4[26:0]), .in_2(bit_extender_2_out[11]), .in_4(and_1_out[11]), .out_7(n27bit_ram_21_out_7),
    .out_6(n27bit_ram_21_out_6), .in_5(in_6), .in_3(in_5));
  _27bit_RAM u_27bit_ram_22 (
    .in_1(in_4[26:0]), .in_2(bit_extender_2_out[10]), .in_4(and_1_out[10]), .out_7(n27bit_ram_22_out_7),
    .out_6(n27bit_ram_22_out_6), .in_5(in_6), .in_3(in_5));
  _27bit_RAM u_27bit_ram_23 (
    .in_1(in_4[26:0]), .in_2(bit_extender_2_out[9]), .in_4(and_1_out[9]), .out_7(n27bit_ram_23_out_7),
    .out_6(n27bit_ram_23_out_6), .in_5(in_6), .in_3(in_5));
  _27bit_RAM u_27bit_ram_24 (
    .in_1(in_4[26:0]), .in_2(bit_extender_2_out[8]), .in_4(and_1_out[8]), .out_7(n27bit_ram_24_out_7),
    .out_6(n27bit_ram_24_out_6), .in_5(in_6), .in_3(in_5));
  _27bit_RAM u_27bit_ram_25 (
    .in_1(in_4[26:0]), .in_2(bit_extender_2_out[7]), .in_4(and_1_out[7]), .out_7(n27bit_ram_25_out_7),
    .out_6(n27bit_ram_25_out_6), .in_5(in_6), .in_3(in_5));
  _27bit_RAM u_27bit_ram_26 (
    .in_1(in_4[26:0]), .in_2(bit_extender_2_out[6]), .in_4(and_1_out[6]), .out_7(n27bit_ram_26_out_7),
    .out_6(n27bit_ram_26_out_6), .in_5(in_6), .in_3(in_5));
  _27bit_RAM u_27bit_ram_27 (
    .in_1(in_4[26:0]), .in_2(bit_extender_2_out[5]), .in_4(and_1_out[5]), .out_7(n27bit_ram_27_out_7),
    .out_6(n27bit_ram_27_out_6), .in_5(in_6), .in_3(in_5));
  _27bit_RAM u_27bit_ram_28 (
    .in_1(in_4[26:0]), .in_2(bit_extender_2_out[4]), .in_4(and_1_out[4]), .out_7(n27bit_ram_28_out_7),
    .out_6(n27bit_ram_28_out_6), .in_5(in_6), .in_3(in_5));
  _27bit_RAM u_27bit_ram_29 (
    .in_1(in_4[26:0]), .in_2(bit_extender_2_out[3]), .in_4(and_1_out[3]), .out_7(n27bit_ram_29_out_7),
    .out_6(n27bit_ram_29_out_6), .in_5(in_6), .in_3(in_5));
  _27bit_RAM u_27bit_ram_30 (
    .in_1(in_4[26:0]), .in_2(bit_extender_2_out[2]), .in_4(and_1_out[2]), .out_7(n27bit_ram_30_out_7),
    .out_6(n27bit_ram_30_out_6), .in_5(in_6), .in_3(in_5));
  _27bit_RAM u_27bit_ram_31 (
    .in_1(in_4[26:0]), .in_2(bit_extender_2_out[1]), .in_4(and_1_out[1]), .out_7(n27bit_ram_31_out_7),
    .out_6(n27bit_ram_31_out_6), .in_5(in_6), .in_3(in_5));
  _27bit_RAM u_27bit_ram_32 (
    .in_1(in_4[26:0]), .in_2(bit_extender_2_out[0]), .in_4(and_1_out[0]), .out_7(n27bit_ram_32_out_7),
    .out_6(n27bit_ram_32_out_6), .in_5(in_6), .in_3(in_5));
  Multiplexer #(.select(5), .width(32), .enable("false")) multiplexer_2 (
    .in0(n27bit_ram_32_out_7), .in1(n27bit_ram_31_out_7), .in2(n27bit_ram_30_out_7),
    .in3(n27bit_ram_29_out_7), .in4(n27bit_ram_28_out_7), .in5(n27bit_ram_27_out_7),
    .in6(n27bit_ram_26_out_7), .in7(n27bit_ram_25_out_7), .in8(n27bit_ram_24_out_7),
    .in9(n27bit_ram_23_out_7), .in10(n27bit_ram_22_out_7), .in11(n27bit_ram_21_out_7),
    .in12(n27bit_ram_20_out_7), .in13(n27bit_ram_19_out_7), .in14(n27bit_ram_18_out_7),
    .in15(n27bit_ram_17_out_7), .in16(n27bit_ram_16_out_7), .in17(n27bit_ram_15_out_7),
    .in18(n27bit_ram_14_out_7), .in19(n27bit_ram_13_out_7), .in20(n27bit_ram_12_out_7),
    .in21(n27bit_ram_11_out_7), .in22(n27bit_ram_10_out_7), .in23(n27bit_ram_9_out_7),
    .in24(n27bit_ram_8_out_7), .in25(n27bit_ram_7_out_7), .in26(n27bit_ram_6_out_7),
    .in27(n27bit_ram_5_out_7), .in28(n27bit_ram_4_out_7), .in29(n27bit_ram_3_out_7),
    .in30(n27bit_ram_2_out_7), .in31(n27bit_ram_1_out_7), .out(out_7), .sel(in_4[31:27]));
  Multiplexer #(.select(5), .width(16), .enable("false")) multiplexer_3 (
    .in0(n27bit_ram_32_out_6), .in1(n27bit_ram_31_out_6), .in2(n27bit_ram_30_out_6),
    .in3(n27bit_ram_29_out_6), .in4(n27bit_ram_28_out_6), .in5(n27bit_ram_27_out_6),
    .in6(n27bit_ram_26_out_6), .in7(n27bit_ram_25_out_6), .in8(n27bit_ram_24_out_6),
    .in9(n27bit_ram_23_out_6), .in10(n27bit_ram_22_out_6), .in11(n27bit_ram_21_out_6),
    .in12(n27bit_ram_20_out_6), .in13(n27bit_ram_19_out_6), .in14(n27bit_ram_18_out_6),
    .in15(n27bit_ram_17_out_6), .in16(n27bit_ram_16_out_6), .in17(n27bit_ram_15_out_6),
    .in18(n27bit_ram_14_out_6), .in19(n27bit_ram_13_out_6), .in20(n27bit_ram_12_out_6),
    .in21(n27bit_ram_11_out_6), .in22(n27bit_ram_10_out_6), .in23(n27bit_ram_9_out_6),
    .in24(n27bit_ram_8_out_6), .in25(n27bit_ram_7_out_6), .in26(n27bit_ram_6_out_6),
    .in27(n27bit_ram_5_out_6), .in28(n27bit_ram_4_out_6), .in29(n27bit_ram_3_out_6),
    .in30(n27bit_ram_2_out_6), .in31(n27bit_ram_1_out_6), .out(out_8), .sel(in_4[31:27]));
endmodule

module mem_read (
  input  [3:0] in_1,
  output out_2
);

  wire comparator_1_eq, comparator_2_eq, comparator_3_eq;

  Comparator #(.width(4), .mode("unsigned")) comparator_1 (
    .a(in_1), .b(4'b1011), .eq(comparator_1_eq));  // open: gt, lt
  Comparator #(.width(4), .mode("unsigned")) comparator_2 (
    .a(in_1), .b(4'b1001), .eq(comparator_2_eq));  // open: gt, lt
  Comparator #(.width(4), .mode("unsigned")) comparator_3 (
    .a(in_1), .b(4'b0101), .eq(comparator_3_eq));  // open: gt, lt
  or or_1 (out_2, comparator_1_eq, comparator_2_eq, comparator_3_eq);
endmodule

module mem_write (
  input  [3:0] in_1,
  output out_2
);

  wire comparator_1_eq, comparator_2_eq, comparator_3_eq;

  Comparator #(.width(4), .mode("unsigned")) comparator_1 (
    .a(in_1), .b(4'b1010), .eq(comparator_1_eq));  // open: gt, lt
  Comparator #(.width(4), .mode("unsigned")) comparator_2 (
    .a(in_1), .b(4'b1000), .eq(comparator_2_eq));  // open: gt, lt
  Comparator #(.width(4), .mode("unsigned")) comparator_3 (
    .a(in_1), .b(4'b0100), .eq(comparator_3_eq));  // open: gt, lt
  or or_1 (out_2, comparator_1_eq, comparator_2_eq, comparator_3_eq);
endmodule

module mem_addr (
  input  [31:0] in_1,
  input  [31:0] in_2,
  input  [3:0] in_3,
  output [31:0] out_4
);

  wire comparator_1_eq, comparator_2_eq, comparator_3_eq, comparator_4_eq, comparator_5_eq, comparator_6_eq,
       or_1_out, or_2_out;
  wire [31:0] multiplexer_2_out, undriven;

  Comparator #(.width(4), .mode("unsigned")) comparator_1 (
    .a(in_3), .b(4'b0100), .eq(comparator_1_eq));  // open: gt, lt
  Comparator #(.width(4), .mode("unsigned")) comparator_2 (
    .a(in_3), .b(4'b0101), .eq(comparator_2_eq));  // open: gt, lt
  Comparator #(.width(4), .mode("unsigned")) comparator_3 (
    .a(in_3), .b(4'b1000), .eq(comparator_3_eq));  // open: gt, lt
  Comparator #(.width(4), .mode("unsigned")) comparator_4 (
    .a(in_3), .b(4'b1010), .eq(comparator_4_eq));  // open: gt, lt
  Comparator #(.width(4), .mode("unsigned")) comparator_5 (
    .a(in_3), .b(4'b1001), .eq(comparator_5_eq));  // open: gt, lt
  Comparator #(.width(4), .mode("unsigned")) comparator_6 (
    .a(in_3), .b(4'b1011), .eq(comparator_6_eq));  // open: gt, lt
  or or_1 (or_1_out, comparator_1_eq, comparator_2_eq, comparator_3_eq, comparator_4_eq);
  or or_2 (or_2_out, comparator_5_eq, comparator_6_eq);
  Multiplexer #(.width(32), .enable("false")) multiplexer_1 (
    .in0(multiplexer_2_out), .in1(in_1), .out(out_4), .sel(or_1_out));
  Multiplexer #(.width(32), .enable("false")) multiplexer_2 (
    .in0(undriven), .in1(in_2), .out(multiplexer_2_out), .sel(or_2_out));
endmodule

module mem_data (
  input  [31:0] in_1,
  input  [31:0] in_2,
  input  [3:0] in_3,
  output [31:0] out_4
);

  wire comparator_1_eq, comparator_2_eq, comparator_3_eq, or_1_out;
  wire [31:0] multiplexer_2_out, undriven;

  Comparator #(.width(4), .mode("unsigned")) comparator_1 (
    .a(in_3), .b(4'b0100), .eq(comparator_1_eq));  // open: gt, lt
  Comparator #(.width(4), .mode("unsigned")) comparator_2 (
    .a(in_3), .b(4'b1010), .eq(comparator_2_eq));  // open: gt, lt
  Comparator #(.width(4), .mode("unsigned")) comparator_3 (
    .a(in_3), .b(4'b1000), .eq(comparator_3_eq));  // open: gt, lt
  or or_1 (or_1_out, comparator_1_eq, comparator_2_eq);
  Multiplexer #(.width(32), .enable("false")) multiplexer_1 (
    .in0(multiplexer_2_out), .in1(in_1), .out(out_4), .sel(or_1_out));
  Multiplexer #(.width(32), .enable("false")) multiplexer_2 (
    .in0(undriven), .in1(in_2), .out(multiplexer_2_out), .sel(comparator_3_eq));
endmodule

module stat (
  input  in_1,
  input  [3:0] in_2,
  output [2:0] out_3
);

  wire comparator_1_eq;
  wire [2:0] multiplexer_2_out;

  Multiplexer #(.width(3), .enable("false")) multiplexer_1 (
    .in0(3'b011), .in1(multiplexer_2_out), .out(out_3), .sel(in_1));
  Multiplexer #(.width(3), .enable("false")) multiplexer_2 (
    .in0(3'b001), .in1(3'b100), .out(multiplexer_2_out), .sel(comparator_1_eq));
  Comparator #(.width(4), .mode("unsigned")) comparator_1 (
    .a(4'b0000), .b(in_2), .eq(comparator_1_eq));  // open: gt, lt
endmodule

module new_pc (
  input  [3:0] in_1,
  input  [31:0] in_2,
  input  in_3,
  input  [31:0] in_4,
  input  [31:0] in_5,
  output [31:0] out_6
);

  wire and_1_out, comparator_1_eq, comparator_2_eq, comparator_3_eq;
  wire [31:0] multiplexer_2_out, multiplexer_3_out;

  Multiplexer #(.width(32), .enable("false")) multiplexer_1 (
    .in0(multiplexer_2_out), .in1(in_2), .out(out_6), .sel(comparator_1_eq));
  Comparator #(.width(4)) comparator_1 (.a(4'b1000), .b(in_1), .eq(comparator_1_eq));  // open: gt, lt
  Comparator #(.width(4)) comparator_2 (.a(4'b0111), .b(in_1), .eq(comparator_2_eq));  // open: gt, lt
  Comparator #(.width(4)) comparator_3 (.a(4'b1001), .b(in_1), .eq(comparator_3_eq));  // open: gt, lt
  and and_1 (and_1_out, comparator_2_eq, in_3);
  Multiplexer #(.width(32), .enable("false")) multiplexer_2 (
    .in0(multiplexer_3_out), .in1(in_2), .out(multiplexer_2_out), .sel(and_1_out));
  Multiplexer #(.width(32), .enable("false")) multiplexer_3 (
    .in0(in_5), .in1(in_4), .out(multiplexer_3_out), .sel(comparator_3_eq));
endmodule

module pc (
  input  in_1,
  input  [31:0] in_2,
  input  in_3,
  output [31:0] out_4
);

  Register #(.width(32)) register_1 (.D(in_2), .en(1'b1), .Q(out_4), .clk(in_3), .clr(in_1));
endmodule

module pc_inc (
  input  in_1,
  input  in_2,
  input  [31:0] in_3,
  output [31:0] out_4
);

  wire [31:0] adder_1_out, adder_2_out, multiplexer_1_out, multiplexer_2_out;

  Multiplexer #(.width(32), .enable("false")) multiplexer_1 (
    .in0({32{1'b0}}), .in1(32'h4), .out(multiplexer_1_out), .sel(in_1));
  Multiplexer #(.width(32), .enable("false")) multiplexer_2 (
    .in0({32{1'b0}}), .in1(32'h1), .out(multiplexer_2_out), .sel(in_2));
  Adder #(.width(32)) adder_1 (.a(multiplexer_1_out), .b(multiplexer_2_out), .out(adder_1_out));  // open: cin, cout
  Adder #(.width(32)) adder_2 (.a(adder_1_out), .b(32'h1), .out(adder_2_out));  // open: cin, cout
  Adder #(.width(32)) adder_3 (.a(adder_2_out), .b(in_3), .out(out_4));  // open: cin, cout
endmodule
